// Logisim project ControlUnit.circ as structural Verilog: 17 circuits, main circuit COMPUTER
module HA (
  input  A,
  input  B,
  output S,
  output Cin
);

  xor xor_1 (S, A, B);
  and and_1 (Cin, A, B);
endmodule

module FA (
  input  A,
  input  B,
  input  Ci,
  output Co,
  output S
);

  wire ha_1_cin, ha_1_s, ha_2_cin;

  HA ha_1 (.B(B), .A(A), .Cin(ha_1_cin), .S(ha_1_s));
  HA ha_2 (.B(Ci), .A(ha_1_s), .Cin(ha_2_cin), .S(S));
  or or_1 (Co, ha_1_cin, ha_2_cin);
endmodule

module FA_16b (
  input  Ci,
  input  [15:0] A,
  input  [15:0] B,
  output [15:0] S,
  output Co
);

  wire fa_1_co, fa_2_co, fa_3_co, fa_4_co, fa_5_co, fa_6_co, fa_7_co, fa_8_co, fa_9_co, fa_10_co, fa_11_co,
       fa_12_co, fa_13_co, fa_14_co, fa_15_co;

  FA fa_1 (.B(B[0]), .Ci(Ci), .A(A[0]), .Co(fa_1_co), .S(S[0]));
  FA fa_2 (.B(B[1]), .Ci(fa_1_co), .A(A[1]), .Co(fa_2_co), .S(S[1]));
  FA fa_3 (.B(B[2]), .Ci(fa_2_co), .A(A[2]), .Co(fa_3_co), .S(S[2]));
  FA fa_4 (.B(B[3]), .Ci(fa_3_co), .A(A[3]), .Co(fa_4_co), .S(S[3]));
  FA fa_5 (.B(B[4]), .Ci(fa_4_co), .A(A[4]), .Co(fa_5_co), .S(S[4]));
  FA fa_6 (.B(B[5]), .Ci(fa_5_co), .A(A[5]), .Co(fa_6_co), .S(S[5]));
  FA fa_7 (.B(B[6]), .Ci(fa_6_co), .A(A[6]), .Co(fa_7_co), .S(S[6]));
  FA fa_8 (.B(B[7]), .Ci(fa_7_co), .A(A[7]), .Co(fa_8_co), .S(S[7]));
  FA fa_9 (.B(B[8]), .Ci(fa_8_co), .A(A[8]), .Co(fa_9_co), .S(S[8]));
  FA fa_10 (.B(B[9]), .Ci(fa_9_co), .A(A[9]), .Co(fa_10_co), .S(S[9]));
  FA fa_11 (.B(B[10]), .Ci(fa_10_co), .A(A[10]), .Co(fa_11_co), .S(S[10]));
  FA fa_12 (.B(B[11]), .Ci(fa_11_co), .A(A[11]), .Co(fa_12_co), .S(S[11]));
  FA fa_13 (.B(B[12]), .Ci(fa_12_co), .A(A[12]), .Co(fa_13_co), .S(S[12]));
  FA fa_14 (.B(B[13]), .Ci(fa_13_co), .A(A[13]), .Co(fa_14_co), .S(S[13]));
  FA fa_15 (.B(B[14]), .Ci(fa_14_co), .A(A[14]), .Co(fa_15_co), .S(S[14]));
  FA fa_16 (.B(B[15]), .Ci(fa_15_co), .A(A[15]), .Co(Co), .S(S[15]));
endmodule

module LU (
  input  [1:0] OP,
  input  [15:0] Y,
  input  [15:0] X,
  output [15:0] S
);

  wire [15:0] and_1_out, not_1_out, or_1_out, xor_1_out;

  assign not_1_out = ~X;  // NOT_Gate not_1, 16 bits wide
  assign and_1_out = X & Y;  // AND_Gate and_1, 16 bits wide
  assign or_1_out = X | Y;  // OR_Gate or_1, 16 bits wide
  Multiplexer #(.select(2), .width(16)) multiplexer_1 (
    .in0(and_1_out), .in1(or_1_out), .in2(xor_1_out), .in3(not_1_out), .out(S));  // open: sel
  assign xor_1_out = X ^ Y;  // XOR_Gate xor_1, 16 bits wide
endmodule

module INV_16b (
  input  [15:0] A,
  input  E,
  output [15:0] S
);

  wire [15:0] not_1_out;

  not not_1 (not_1_out[0], A[0]);
  not not_2 (not_1_out[1], A[1]);
  not not_3 (not_1_out[2], A[2]);
  not not_4 (not_1_out[3], A[3]);
  not not_5 (not_1_out[4], A[4]);
  not not_6 (not_1_out[5], A[5]);
  not not_7 (not_1_out[6], A[6]);
  not not_8 (not_1_out[7], A[7]);
  not not_9 (not_1_out[8], A[8]);
  not not_10 (not_1_out[9], A[9]);
  not not_11 (not_1_out[10], A[10]);
  not not_12 (not_1_out[11], A[11]);
  not not_13 (not_1_out[12], A[12]);
  not not_14 (not_1_out[13], A[13]);
  not not_15 (not_1_out[14], A[14]);
  not not_16 (not_1_out[15], A[15]);
  LED INV_ENABLED (.in(E));
  Multiplexer #(.width(16)) multiplexer_1 (.in0(A), .in1(not_1_out), .out(S), .sel(E));
endmodule

module XOR_16b (
  input  [15:0] A,
  input  [15:0] B,
  output [15:0] S
);

  xor xor_1 (S[0], A[0], B[0]);
  xor xor_2 (S[1], A[1], B[1]);
  xor xor_3 (S[2], A[2], B[2]);
  xor xor_4 (S[3], A[3], B[3]);
  xor xor_5 (S[4], A[4], B[4]);
  xor xor_6 (S[5], A[5], B[5]);
  xor xor_7 (S[6], A[6], B[6]);
  xor xor_8 (S[7], A[7], B[7]);
  xor xor_9 (S[8], A[8], B[8]);
  xor xor_10 (S[9], A[9], B[9]);
  xor xor_11 (S[10], A[10], B[10]);
  xor xor_12 (S[11], A[11], B[11]);
  xor xor_13 (S[12], A[12], B[12]);
  xor xor_14 (S[13], A[13], B[13]);
  xor xor_15 (S[14], A[14], B[14]);
  xor xor_16 (S[15], A[15], B[15]);
endmodule

module OR_16b (
  input  [15:0] A,
  input  [15:0] B,
  output [15:0] S
);

  or or_1 (S[0], A[0], B[0]);
  or or_2 (S[1], A[1], B[1]);
  or or_3 (S[2], A[2], B[2]);
  or or_4 (S[3], A[3], B[3]);
  or or_5 (S[4], A[4], B[4]);
  or or_6 (S[5], A[5], B[5]);
  or or_7 (S[6], A[6], B[6]);
  or or_8 (S[7], A[7], B[7]);
  or or_9 (S[8], A[8], B[8]);
  or or_10 (S[9], A[9], B[9]);
  or or_11 (S[10], A[10], B[10]);
  or or_12 (S[11], A[11], B[11]);
  or or_13 (S[12], A[12], B[12]);
  or or_14 (S[13], A[13], B[13]);
  or or_15 (S[14], A[14], B[14]);
  or or_16 (S[15], A[15], B[15]);
endmodule

module AND_16b (
  input  [15:0] A,
  input  [15:0] B,
  output [15:0] S
);

  and and_1 (S[0], A[0], B[0]);
  and and_2 (S[1], A[1], B[1]);
  and and_3 (S[2], A[2], B[2]);
  and and_4 (S[3], A[3], B[3]);
  and and_5 (S[4], A[4], B[4]);
  and and_6 (S[5], A[5], B[5]);
  and and_7 (S[6], A[6], B[6]);
  and and_8 (S[7], A[7], B[7]);
  and and_9 (S[8], A[8], B[8]);
  and and_10 (S[9], A[9], B[9]);
  and and_11 (S[10], A[10], B[10]);
  and and_12 (S[11], A[11], B[11]);
  and and_13 (S[12], A[12], B[12]);
  and and_14 (S[13], A[13], B[13]);
  and and_15 (S[14], A[14], B[14]);
  and and_16 (S[15], A[15], B[15]);
endmodule

module AU (
  input  [1:0] OP,
  input  [15:0] X,
  input  [15:0] Y,
  output [15:0] S
);

  wire [15:0] inv_16b_1_s, multiplexer_1_p4;

  // Multiplexer #(.width(16)) multiplexer_1: pin names not known; wires that end beside it: Y, 16'h1, OP[0], multiplexer_1_p4
  INV_16b inv_16b_1 (.E(OP[1]), .A(multiplexer_1_p4), .S(inv_16b_1_s));
  FA_16b fa_16b_1 (.Ci(OP[1]), .A(X), .B(inv_16b_1_s), .S(S));  // open: Co
endmodule

module ALU (
  input  Sw,
  input  Zx,
  input  U,
  input  [1:0] OP,
  input  [15:0] X,
  input  [15:0] Y,
  output [15:0] S
);

  wire [15:0] au_1_s, lu_1_s, multiplexer_1_out, swap_16b_1_x, swap_16b_1_y;

  Multiplexer #(.width(16)) multiplexer_1 (.in0(swap_16b_1_x), .in1({16{1'b0}}), .out(multiplexer_1_out), .sel(Zx));
  SWAP_16b swap_16b_1 (.E(Sw), .A(X), .B(Y), .X(swap_16b_1_x), .Y(swap_16b_1_y));
  LU lu_1 (.OP(OP), .Y(swap_16b_1_y), .X(multiplexer_1_out), .S(lu_1_s));
  Multiplexer #(.width(16)) multiplexer_2 (.in0(lu_1_s), .in1(au_1_s), .out(S));  // open: sel
  AU au_1 (.OP(OP), .X(multiplexer_1_out), .Y(swap_16b_1_y), .S(au_1_s));
endmodule

module SWAP_16b (
  input  [15:0] A,
  input  [15:0] B,
  input  E,
  output [15:0] X,
  output [15:0] Y
);

  LED SWAP_ENABLE (.in(E));
  Multiplexer #(.width(16)) multiplexer_1 (.in0(A), .in1(B), .out(X), .sel(E));
  Multiplexer #(.width(16)) multiplexer_2 (.in0(B), .in1(A), .out(Y), .sel(E));
endmodule

module EQZ_16b (
  input  [15:0] A,
  output S
);

  wire [15:0] not_1_out;

  assign not_1_out = ~A;  // NOT_Gate not_1, 16 bits wide
  and and_1 (S, not_1_out[0], not_1_out[1], not_1_out[2], not_1_out[3], not_1_out[4], not_1_out[5], not_1_out[6], not_1_out[7], not_1_out[8], not_1_out[9], not_1_out[10], not_1_out[11], not_1_out[12], not_1_out[13], not_1_out[14], not_1_out[15]);
  LED EQUAL_ZERO (.in(S));
endmodule

module FLAG (
  input  GT,
  input  EQ,
  input  LT,
  input  [15:0] X,
  output S
);

  wire and_1_out, and_2_out, and_3_out, and_4_out, eqz_16b_1_s, not_1_out, not_2_out;

  and and_1 (and_1_out, not_1_out, not_2_out);
  not not_1 (not_1_out, X[15]);
  not not_2 (not_2_out, eqz_16b_1_s);
  and and_2 (and_2_out, GT, and_1_out);
  and and_3 (and_3_out, LT, X[15]);
  or or_1 (S, and_2_out, and_3_out, and_4_out);
  and and_4 (and_4_out, EQ, eqz_16b_1_s);
  EQZ_16b eqz_16b_1 (.A(X), .S(eqz_16b_1_s));
endmodule

module MEMORY (
  input  [15:0] X,
  input  A,
  input  D,
  input  R,
  input  CLK,
  output [15:0] DA,
  output [15:0] DD,
  output [15:0] DR
);

  wire button_1_out, t_box_1_s;
  wire [8:0] hex_disp_dec_1_l0, hex_disp_dec_1_l1, hex_disp_dec_1_l2, hex_disp_dec_1_l3, hex_disp_dec_1_l4,
       hex_disp_dec_2_l0, hex_disp_dec_2_l1, hex_disp_dec_2_l2, hex_disp_dec_2_l3, hex_disp_dec_2_l4,
       hex_disp_dec_3_l0, hex_disp_dec_3_l1, hex_disp_dec_3_l2, hex_disp_dec_3_l3, hex_disp_dec_3_l4,
       hex_disp_dec_4_l0, hex_disp_dec_4_l1, hex_disp_dec_4_l2, hex_disp_dec_4_l3, hex_disp_dec_4_l4,
       hex_disp_dec_5_l0, hex_disp_dec_5_l1, hex_disp_dec_5_l2, hex_disp_dec_5_l3, hex_disp_dec_5_l4,
       hex_disp_dec_6_l0, hex_disp_dec_6_l1, hex_disp_dec_6_l2, hex_disp_dec_6_l3, hex_disp_dec_6_l4,
       hex_disp_dec_7_l0, hex_disp_dec_7_l1, hex_disp_dec_7_l2, hex_disp_dec_7_l3, hex_disp_dec_7_l4,
       hex_disp_dec_8_l0, hex_disp_dec_8_l1, hex_disp_dec_8_l2, hex_disp_dec_8_l3, hex_disp_dec_8_l4,
       hex_disp_dec_9_l0, hex_disp_dec_9_l1, hex_disp_dec_9_l2, hex_disp_dec_9_l3, hex_disp_dec_9_l4,
       hex_disp_dec_10_l0, hex_disp_dec_10_l1, hex_disp_dec_10_l2, hex_disp_dec_10_l3, hex_disp_dec_10_l4,
       hex_disp_dec_11_l0, hex_disp_dec_11_l1, hex_disp_dec_11_l2, hex_disp_dec_11_l3, hex_disp_dec_11_l4,
       hex_disp_dec_12_l0, hex_disp_dec_12_l1, hex_disp_dec_12_l2, hex_disp_dec_12_l3, hex_disp_dec_12_l4;

  Register #(.width(16)) REG_A (.D(X), .en(A), .clk(CLK), .Q(DA));  // open: clr
  Register #(.width(16)) REG_D (.D(X), .en(D), .clk(CLK), .Q(DD));  // open: clr
  RAM #(.addrWidth(16), .asyncread("true"), .dataWidth(16)) ram_1 (
    .addr(DA), .we(R), .clk(CLK), .din(X), .dout(DR));  // open: oe
  DotMatrix #(.matrixrows(9)) dotmatrix_1 (
    .col0(hex_disp_dec_1_l0), .col1(hex_disp_dec_1_l1), .col2(hex_disp_dec_1_l2), .col3(hex_disp_dec_1_l3),
    .col4(hex_disp_dec_1_l4));
  HEX_DISP_DEC hex_disp_dec_1 (
    .BIN(DA[15:12]), .E(t_box_1_s), .L3(hex_disp_dec_1_l3), .L4(hex_disp_dec_1_l4), .L0(hex_disp_dec_1_l0),
    .L1(hex_disp_dec_1_l1), .L2(hex_disp_dec_1_l2));
  // Probe on DA
  DotMatrix #(.matrixrows(9)) dotmatrix_2 (
    .col0(hex_disp_dec_2_l0), .col1(hex_disp_dec_2_l1), .col2(hex_disp_dec_2_l2), .col3(hex_disp_dec_2_l3),
    .col4(hex_disp_dec_2_l4));
  HEX_DISP_DEC hex_disp_dec_2 (
    .BIN(DD[15:12]), .E(t_box_1_s), .L3(hex_disp_dec_2_l3), .L4(hex_disp_dec_2_l4), .L0(hex_disp_dec_2_l0),
    .L1(hex_disp_dec_2_l1), .L2(hex_disp_dec_2_l2));
  // Probe on DD
  DotMatrix #(.matrixrows(9)) dotmatrix_3 (
    .col0(hex_disp_dec_3_l0), .col1(hex_disp_dec_3_l1), .col2(hex_disp_dec_3_l2), .col3(hex_disp_dec_3_l3),
    .col4(hex_disp_dec_3_l4));
  HEX_DISP_DEC hex_disp_dec_3 (
    .BIN(DR[15:12]), .E(t_box_1_s), .L3(hex_disp_dec_3_l3), .L4(hex_disp_dec_3_l4), .L0(hex_disp_dec_3_l0),
    .L1(hex_disp_dec_3_l1), .L2(hex_disp_dec_3_l2));
  // Probe on DR
  DotMatrix #(.matrixrows(9)) dotmatrix_4 (
    .col0(hex_disp_dec_4_l0), .col1(hex_disp_dec_4_l1), .col2(hex_disp_dec_4_l2), .col3(hex_disp_dec_4_l3),
    .col4(hex_disp_dec_4_l4));
  HEX_DISP_DEC hex_disp_dec_4 (
    .BIN(DA[11:8]), .E(t_box_1_s), .L3(hex_disp_dec_4_l3), .L4(hex_disp_dec_4_l4), .L0(hex_disp_dec_4_l0),
    .L1(hex_disp_dec_4_l1), .L2(hex_disp_dec_4_l2));
  DotMatrix #(.matrixrows(9)) dotmatrix_5 (
    .col0(hex_disp_dec_5_l0), .col1(hex_disp_dec_5_l1), .col2(hex_disp_dec_5_l2), .col3(hex_disp_dec_5_l3),
    .col4(hex_disp_dec_5_l4));
  HEX_DISP_DEC hex_disp_dec_5 (
    .BIN(DD[11:8]), .E(t_box_1_s), .L3(hex_disp_dec_5_l3), .L4(hex_disp_dec_5_l4), .L0(hex_disp_dec_5_l0),
    .L1(hex_disp_dec_5_l1), .L2(hex_disp_dec_5_l2));
  DotMatrix #(.matrixrows(9)) dotmatrix_6 (
    .col0(hex_disp_dec_6_l0), .col1(hex_disp_dec_6_l1), .col2(hex_disp_dec_6_l2), .col3(hex_disp_dec_6_l3),
    .col4(hex_disp_dec_6_l4));
  HEX_DISP_DEC hex_disp_dec_6 (
    .BIN(DR[11:8]), .E(t_box_1_s), .L3(hex_disp_dec_6_l3), .L4(hex_disp_dec_6_l4), .L0(hex_disp_dec_6_l0),
    .L1(hex_disp_dec_6_l1), .L2(hex_disp_dec_6_l2));
  DotMatrix #(.matrixrows(9)) dotmatrix_7 (
    .col0(hex_disp_dec_7_l0), .col1(hex_disp_dec_7_l1), .col2(hex_disp_dec_7_l2), .col3(hex_disp_dec_7_l3),
    .col4(hex_disp_dec_7_l4));
  DotMatrix #(.matrixrows(9)) dotmatrix_8 (
    .col0(hex_disp_dec_8_l0), .col1(hex_disp_dec_8_l1), .col2(hex_disp_dec_8_l2), .col3(hex_disp_dec_8_l3),
    .col4(hex_disp_dec_8_l4));
  HEX_DISP_DEC hex_disp_dec_7 (
    .BIN(DA[7:4]), .E(t_box_1_s), .L3(hex_disp_dec_7_l3), .L4(hex_disp_dec_7_l4), .L0(hex_disp_dec_7_l0),
    .L1(hex_disp_dec_7_l1), .L2(hex_disp_dec_7_l2));
  HEX_DISP_DEC hex_disp_dec_8 (
    .BIN(DA[3:0]), .E(t_box_1_s), .L3(hex_disp_dec_8_l3), .L4(hex_disp_dec_8_l4), .L0(hex_disp_dec_8_l0),
    .L1(hex_disp_dec_8_l1), .L2(hex_disp_dec_8_l2));
  DotMatrix #(.matrixrows(9)) dotmatrix_9 (
    .col0(hex_disp_dec_9_l0), .col1(hex_disp_dec_9_l1), .col2(hex_disp_dec_9_l2), .col3(hex_disp_dec_9_l3),
    .col4(hex_disp_dec_9_l4));
  DotMatrix #(.matrixrows(9)) dotmatrix_10 (
    .col0(hex_disp_dec_10_l0), .col1(hex_disp_dec_10_l1), .col2(hex_disp_dec_10_l2),
    .col3(hex_disp_dec_10_l3), .col4(hex_disp_dec_10_l4));
  HEX_DISP_DEC hex_disp_dec_9 (
    .BIN(DD[7:4]), .E(t_box_1_s), .L3(hex_disp_dec_9_l3), .L4(hex_disp_dec_9_l4), .L0(hex_disp_dec_9_l0),
    .L1(hex_disp_dec_9_l1), .L2(hex_disp_dec_9_l2));
  HEX_DISP_DEC hex_disp_dec_10 (
    .BIN(DD[3:0]), .E(t_box_1_s), .L3(hex_disp_dec_10_l3), .L4(hex_disp_dec_10_l4), .L0(hex_disp_dec_10_l0),
    .L1(hex_disp_dec_10_l1), .L2(hex_disp_dec_10_l2));
  DotMatrix #(.matrixrows(9)) dotmatrix_11 (
    .col0(hex_disp_dec_11_l0), .col1(hex_disp_dec_11_l1), .col2(hex_disp_dec_11_l2),
    .col3(hex_disp_dec_11_l3), .col4(hex_disp_dec_11_l4));
  DotMatrix #(.matrixrows(9)) dotmatrix_12 (
    .col0(hex_disp_dec_12_l0), .col1(hex_disp_dec_12_l1), .col2(hex_disp_dec_12_l2),
    .col3(hex_disp_dec_12_l3), .col4(hex_disp_dec_12_l4));
  HEX_DISP_DEC hex_disp_dec_11 (
    .BIN(DR[7:4]), .E(t_box_1_s), .L3(hex_disp_dec_11_l3), .L4(hex_disp_dec_11_l4), .L0(hex_disp_dec_11_l0),
    .L1(hex_disp_dec_11_l1), .L2(hex_disp_dec_11_l2));
  HEX_DISP_DEC hex_disp_dec_12 (
    .BIN(DR[3:0]), .E(t_box_1_s), .L3(hex_disp_dec_12_l3), .L4(hex_disp_dec_12_l4), .L0(hex_disp_dec_12_l0),
    .L1(hex_disp_dec_12_l1), .L2(hex_disp_dec_12_l2));
  Button button_1 (.out(button_1_out));
  T_BOX t_box_1 (.T(button_1_out), .S(t_box_1_s));
  HEX_DISP_16b hex_disp_16b_1 (.A(DA));
  HEX_DISP_16b hex_disp_16b_2 (.A(DD));
  HEX_DISP_16b hex_disp_16b_3 (.A(DR));

  // Notes on the sheet:
  //   REG_A
  //   REG_D
  //   RAM
endmodule

module ALU_INST (
  input  [15:0] D,
  input  [15:0] A,
  input  [15:0] R,
  input  [15:0] OP,
  output DA,
  output DD,
  output DR,
  output J,
  output [15:0] S
);

  wire [15:0] multiplexer_1_out;

  FLAG flag_1 (.GT(OP[0]), .EQ(OP[1]), .LT(OP[2]), .X(S), .S(J));
  ALU alu_1 (.X(D), .Y(multiplexer_1_out), .Sw(OP[6]), .Zx(OP[7]), .OP(OP[9:8]), .U(OP[10]), .S(S));
  Multiplexer #(.width(16)) multiplexer_1 (.in0(A), .in1(R), .out(multiplexer_1_out));  // open: sel

  assign DA = OP[5];
  assign DD = OP[4];
  assign DR = OP[3];
endmodule

module CU (
  input  [15:0] OP,
  input  [15:0] A,
  input  [15:0] D,
  input  [15:0] R,
  output DA,
  output DD,
  output DR,
  output J,
  output [15:0] S
);

  wire alu_inst_1_da, alu_inst_1_dd, alu_inst_1_dr, alu_inst_1_j, not_1_out;
  wire [15:0] alu_inst_1_s;

  nand nand_1 (DA, OP[15], not_1_out);
  and and_1 (DD, OP[15], alu_inst_1_dd);
  not not_1 (not_1_out, alu_inst_1_da);
  and and_2 (DR, OP[15], alu_inst_1_dr);
  and and_3 (J, OP[15], alu_inst_1_j);
  ALU_INST alu_inst_1 (
    .OP(OP), .D(D), .A(A), .R(R), .DA(alu_inst_1_da), .DD(alu_inst_1_dd), .DR(alu_inst_1_dr),
    .S(alu_inst_1_s), .J(alu_inst_1_j));
  Multiplexer #(.width(16)) multiplexer_1 (.in0(OP), .in1(alu_inst_1_s), .out(S));  // open: sel
endmodule

module COMPUTER (
);

  wire button_1_out, CLK_ENABLE_out, CLK_OVERLOAD_out, clock_1_out, COUNTER_RESET_out, cu_1_da, cu_1_dd,
       cu_1_dr, cu_1_j, multiplexer_1_out, t_box_1_s, t_box_2_s;
  wire [3:0] rom_1_data, rom_1_data_2, rom_1_data_3, rom_1_data_4;
  wire [8:0] hex_disp_dec_1_l0, hex_disp_dec_1_l1, hex_disp_dec_1_l2, hex_disp_dec_1_l3, hex_disp_dec_1_l4,
       hex_disp_dec_2_l0, hex_disp_dec_2_l1, hex_disp_dec_2_l2, hex_disp_dec_2_l3, hex_disp_dec_2_l4,
       hex_disp_dec_3_l0, hex_disp_dec_3_l1, hex_disp_dec_3_l2, hex_disp_dec_3_l3, hex_disp_dec_3_l4,
       hex_disp_dec_4_l0, hex_disp_dec_4_l1, hex_disp_dec_4_l2, hex_disp_dec_4_l3, hex_disp_dec_4_l4;
  wire [15:0] counter_1_q, cu_1_s;
  wire [47:0] memory_1_da;

  Button COUNTER_RESET (.out(COUNTER_RESET_out));
  Button CLK_ENABLE (.out(CLK_ENABLE_out));
  Button CLK_OVERLOAD (.out(CLK_OVERLOAD_out));
  Clock clock_1 (.out(clock_1_out));
  Counter #(.max('hffff), .trigger("falling"), .width(16)) counter_1 (
    .clr(COUNTER_RESET_out), .load(cu_1_j), .clk(multiplexer_1_out), .D(memory_1_da[15:0]), .Q(counter_1_q));  // open: up, count, carry
  T_BOX t_box_1 (.T(CLK_ENABLE_out), .S(t_box_1_s));
  Multiplexer multiplexer_1 (.in0(CLK_OVERLOAD_out), .in1(clock_1_out), .out(multiplexer_1_out));  // open: sel
  MEMORY memory_1 (
    .A(cu_1_da), .D(cu_1_dd), .R(cu_1_dr), .CLK(multiplexer_1_out), .X(cu_1_s), .DA(memory_1_da[15:0]),
    .DD(memory_1_da[31:16]), .DR(memory_1_da[47:32]));
  CU cu_1 (
    .OP({rom_1_data_4, rom_1_data_3, rom_1_data_2, rom_1_data}), .A(memory_1_da[15:0]),
    .D(memory_1_da[31:16]), .R(memory_1_da[47:32]), .DA(cu_1_da), .DD(cu_1_dd), .DR(cu_1_dr), .J(cu_1_j),
    .S(cu_1_s));
  ROM #(.addrWidth(16), .dataWidth(16)) rom_1 (
    .addr(counter_1_q), .data({rom_1_data_4, rom_1_data_3, rom_1_data_2, rom_1_data}));
  DotMatrix #(.matrixrows(9)) dotmatrix_1 (
    .col0(hex_disp_dec_1_l0), .col1(hex_disp_dec_1_l1), .col2(hex_disp_dec_1_l2), .col3(hex_disp_dec_1_l3),
    .col4(hex_disp_dec_1_l4));
  HEX_DISP_DEC hex_disp_dec_1 (
    .BIN(rom_1_data_4), .E(t_box_2_s), .L3(hex_disp_dec_1_l3), .L4(hex_disp_dec_1_l4),
    .L0(hex_disp_dec_1_l0), .L1(hex_disp_dec_1_l1), .L2(hex_disp_dec_1_l2));
  DotMatrix #(.matrixrows(9)) dotmatrix_2 (
    .col0(hex_disp_dec_2_l0), .col1(hex_disp_dec_2_l1), .col2(hex_disp_dec_2_l2), .col3(hex_disp_dec_2_l3),
    .col4(hex_disp_dec_2_l4));
  HEX_DISP_DEC hex_disp_dec_2 (
    .BIN(rom_1_data_3), .E(t_box_2_s), .L3(hex_disp_dec_2_l3), .L4(hex_disp_dec_2_l4),
    .L0(hex_disp_dec_2_l0), .L1(hex_disp_dec_2_l1), .L2(hex_disp_dec_2_l2));
  DotMatrix #(.matrixrows(9)) dotmatrix_3 (
    .col0(hex_disp_dec_3_l0), .col1(hex_disp_dec_3_l1), .col2(hex_disp_dec_3_l2), .col3(hex_disp_dec_3_l3),
    .col4(hex_disp_dec_3_l4));
  DotMatrix #(.matrixrows(9)) dotmatrix_4 (
    .col0(hex_disp_dec_4_l0), .col1(hex_disp_dec_4_l1), .col2(hex_disp_dec_4_l2), .col3(hex_disp_dec_4_l3),
    .col4(hex_disp_dec_4_l4));
  HEX_DISP_DEC hex_disp_dec_3 (
    .BIN(rom_1_data_2), .E(t_box_2_s), .L3(hex_disp_dec_3_l3), .L4(hex_disp_dec_3_l4),
    .L0(hex_disp_dec_3_l0), .L1(hex_disp_dec_3_l1), .L2(hex_disp_dec_3_l2));
  HEX_DISP_DEC hex_disp_dec_4 (
    .BIN(rom_1_data), .E(t_box_2_s), .L3(hex_disp_dec_4_l3), .L4(hex_disp_dec_4_l4), .L0(hex_disp_dec_4_l0),
    .L1(hex_disp_dec_4_l1), .L2(hex_disp_dec_4_l2));
  Button button_1 (.out(button_1_out));
  T_BOX t_box_2 (.T(button_1_out), .S(t_box_2_s));

  // Notes on the sheet:
  //   contents of rom_1 (hex, n*v repeats v):
  //   1234 8490 0 84c8 5 8007
endmodule
