// Logisim project Misc.circ as structural Verilog: 9 circuits, main circuit HEX_DISP_DEC
module test (
  input  [7:0] A2,
  input  [15:0] A_16b,
  input  [31:0] in_3
);

  wire button_1_out, button_2_out, button_3_out, dec_disp_dec_1_a, dec_disp_dec_1_b, dec_disp_dec_1_c,
       dec_disp_dec_1_d, dec_disp_dec_1_e, dec_disp_dec_1_f, dec_disp_dec_1_g, dec_disp_dec_2_a,
       dec_disp_dec_2_b, dec_disp_dec_2_c, dec_disp_dec_2_d, dec_disp_dec_2_e, dec_disp_dec_2_f,
       dec_disp_dec_2_g, dec_disp_dec_3_a, dec_disp_dec_3_b, dec_disp_dec_3_c, dec_disp_dec_3_d,
       dec_disp_dec_3_e, dec_disp_dec_3_f, dec_disp_dec_3_g, dec_disp_dec_4_a, dec_disp_dec_4_b,
       dec_disp_dec_4_c, dec_disp_dec_4_d, dec_disp_dec_4_e, dec_disp_dec_4_f, dec_disp_dec_4_g,
       dec_disp_dec_5_a, dec_disp_dec_5_b, dec_disp_dec_5_c, dec_disp_dec_5_d, dec_disp_dec_5_e,
       dec_disp_dec_5_f, dec_disp_dec_5_g, dec_disp_dec_6_a, dec_disp_dec_6_b, dec_disp_dec_6_c,
       dec_disp_dec_6_d, dec_disp_dec_6_e, dec_disp_dec_6_f, dec_disp_dec_6_g, dec_disp_dec_7_a,
       dec_disp_dec_7_b, dec_disp_dec_7_c, dec_disp_dec_7_d, dec_disp_dec_7_e, dec_disp_dec_7_f,
       dec_disp_dec_7_g, dec_disp_dec_8_a, dec_disp_dec_8_b, dec_disp_dec_8_c, dec_disp_dec_8_d,
       dec_disp_dec_8_e, dec_disp_dec_8_f, dec_disp_dec_8_g, dec_disp_dec_9_a, dec_disp_dec_9_b,
       dec_disp_dec_9_c, dec_disp_dec_9_d, dec_disp_dec_9_e, dec_disp_dec_9_f, dec_disp_dec_9_g,
       dec_disp_dec_10_a, dec_disp_dec_10_b, dec_disp_dec_10_c, dec_disp_dec_10_d, dec_disp_dec_10_e,
       dec_disp_dec_10_f, dec_disp_dec_10_g, dec_disp_dec_11_a, dec_disp_dec_11_b, dec_disp_dec_11_c,
       dec_disp_dec_11_d, dec_disp_dec_11_e, dec_disp_dec_11_f, dec_disp_dec_11_g, dec_disp_dec_12_a,
       dec_disp_dec_12_b, dec_disp_dec_12_c, dec_disp_dec_12_d, dec_disp_dec_12_e, dec_disp_dec_12_f,
       dec_disp_dec_12_g, dec_disp_dec_13_a, dec_disp_dec_13_b, dec_disp_dec_13_c, dec_disp_dec_13_d,
       dec_disp_dec_13_e, dec_disp_dec_13_f, dec_disp_dec_13_g, dec_disp_dec_14_a, dec_disp_dec_14_b,
       dec_disp_dec_14_c, dec_disp_dec_14_d, dec_disp_dec_14_e, dec_disp_dec_14_f, dec_disp_dec_14_g,
       dec_disp_dec_15_a, dec_disp_dec_15_b, dec_disp_dec_15_c, dec_disp_dec_15_d, dec_disp_dec_15_e,
       dec_disp_dec_15_f, dec_disp_dec_15_g, dec_disp_dec_16_a, dec_disp_dec_16_b, dec_disp_dec_16_c,
       dec_disp_dec_16_d, dec_disp_dec_16_e, dec_disp_dec_16_f, dec_disp_dec_16_g, dec_disp_dec_17_a,
       dec_disp_dec_17_b, dec_disp_dec_17_c, dec_disp_dec_17_d, dec_disp_dec_17_e, dec_disp_dec_17_f,
       dec_disp_dec_17_g, dec_disp_dec_18_a, dec_disp_dec_18_b, dec_disp_dec_18_c, dec_disp_dec_18_d,
       dec_disp_dec_18_e, dec_disp_dec_18_f, dec_disp_dec_18_g, t_box_1_s, t_box_2_s, t_box_3_s;
  wire [1:0] dd_8b_1_p8_9;
  wire [3:0] dd_8b_1_p0_3, dd_8b_1_p4_7, dd_16b_1_p0_3, dd_16b_1_p4_7, dd_16b_1_p8_11, dd_16b_1_p12_15,
       dd_16b_1_p16_19, dd_32b_1_p0_3, dd_32b_1_p4_7, dd_32b_1_p8_11, dd_32b_1_p12_15, dd_32b_1_p16_19,
       dd_32b_1_p20_23, dd_32b_1_p24_27, dd_32b_1_p28_31, dd_32b_1_p32_35, dd_32b_1_p36_39;

  Button button_1 (.out(button_1_out));
  Button button_2 (.out(button_2_out));
  Button button_3 (.out(button_3_out));
  _7_Segment_Display #(.decimalPoint("false")) u_7_segment_display_1 (
    .g(dec_disp_dec_1_g), .f(dec_disp_dec_1_f), .a(dec_disp_dec_1_a), .b(dec_disp_dec_1_b),
    .e(dec_disp_dec_1_e), .d(dec_disp_dec_1_d), .c(dec_disp_dec_1_c));
  DEC_DISP_DEC dec_disp_dec_1 (
    .En(t_box_1_s), .X({2'b00, dd_8b_1_p8_9}), .B(dec_disp_dec_1_b), .C(dec_disp_dec_1_c),
    .D(dec_disp_dec_1_d), .E(dec_disp_dec_1_e), .F(dec_disp_dec_1_f), .G(dec_disp_dec_1_g),
    .A(dec_disp_dec_1_a));
  T_BOX t_box_1 (.T(button_1_out), .S(t_box_1_s));
  DD_8b dd_8b_1 (.A(A2), .P4_7(dd_8b_1_p4_7), .P0_3(dd_8b_1_p0_3), .P8_9(dd_8b_1_p8_9));
  T_BOX t_box_2 (.T(button_2_out), .S(t_box_2_s));
  T_BOX t_box_3 (.T(button_3_out), .S(t_box_3_s));
  _7_Segment_Display #(.decimalPoint("false")) u_7_segment_display_2 (
    .g(dec_disp_dec_2_g), .f(dec_disp_dec_2_f), .a(dec_disp_dec_2_a), .b(dec_disp_dec_2_b),
    .e(dec_disp_dec_2_e), .d(dec_disp_dec_2_d), .c(dec_disp_dec_2_c));
  _7_Segment_Display #(.decimalPoint("false")) u_7_segment_display_3 (
    .g(dec_disp_dec_3_g), .f(dec_disp_dec_3_f), .a(dec_disp_dec_3_a), .b(dec_disp_dec_3_b),
    .e(dec_disp_dec_3_e), .d(dec_disp_dec_3_d), .c(dec_disp_dec_3_c));
  DEC_DISP_DEC dec_disp_dec_2 (
    .En(t_box_1_s), .X(dd_8b_1_p4_7), .B(dec_disp_dec_2_b), .C(dec_disp_dec_2_c), .D(dec_disp_dec_2_d),
    .E(dec_disp_dec_2_e), .F(dec_disp_dec_2_f), .G(dec_disp_dec_2_g), .A(dec_disp_dec_2_a));
  DEC_DISP_DEC dec_disp_dec_3 (
    .En(t_box_1_s), .X(dd_8b_1_p0_3), .B(dec_disp_dec_3_b), .C(dec_disp_dec_3_c), .D(dec_disp_dec_3_d),
    .E(dec_disp_dec_3_e), .F(dec_disp_dec_3_f), .G(dec_disp_dec_3_g), .A(dec_disp_dec_3_a));
  _7_Segment_Display #(.decimalPoint("false")) u_7_segment_display_4 (
    .g(dec_disp_dec_4_g), .f(dec_disp_dec_4_f), .a(dec_disp_dec_4_a), .b(dec_disp_dec_4_b),
    .e(dec_disp_dec_4_e), .d(dec_disp_dec_4_d), .c(dec_disp_dec_4_c));
  _7_Segment_Display #(.decimalPoint("false")) u_7_segment_display_5 (
    .g(dec_disp_dec_5_g), .f(dec_disp_dec_5_f), .a(dec_disp_dec_5_a), .b(dec_disp_dec_5_b),
    .e(dec_disp_dec_5_e), .d(dec_disp_dec_5_d), .c(dec_disp_dec_5_c));
  DEC_DISP_DEC dec_disp_dec_4 (
    .En(t_box_2_s), .X(dd_16b_1_p16_19), .B(dec_disp_dec_4_b), .C(dec_disp_dec_4_c), .D(dec_disp_dec_4_d),
    .E(dec_disp_dec_4_e), .F(dec_disp_dec_4_f), .G(dec_disp_dec_4_g), .A(dec_disp_dec_4_a));
  DEC_DISP_DEC dec_disp_dec_5 (
    .En(t_box_2_s), .X(dd_16b_1_p12_15), .B(dec_disp_dec_5_b), .C(dec_disp_dec_5_c), .D(dec_disp_dec_5_d),
    .E(dec_disp_dec_5_e), .F(dec_disp_dec_5_f), .G(dec_disp_dec_5_g), .A(dec_disp_dec_5_a));
  DD_16b dd_16b_1 (
    .A(A_16b), .P0_3(dd_16b_1_p0_3), .P4_7(dd_16b_1_p4_7), .P8_11(dd_16b_1_p8_11), .P12_15(dd_16b_1_p12_15),
    .P16_19(dd_16b_1_p16_19));
  _7_Segment_Display #(.decimalPoint("false")) u_7_segment_display_6 (
    .g(dec_disp_dec_6_g), .f(dec_disp_dec_6_f), .a(dec_disp_dec_6_a), .b(dec_disp_dec_6_b),
    .e(dec_disp_dec_6_e), .d(dec_disp_dec_6_d), .c(dec_disp_dec_6_c));
  DEC_DISP_DEC dec_disp_dec_6 (
    .En(t_box_3_s), .X(dd_32b_1_p36_39), .B(dec_disp_dec_6_b), .C(dec_disp_dec_6_c), .D(dec_disp_dec_6_d),
    .E(dec_disp_dec_6_e), .F(dec_disp_dec_6_f), .G(dec_disp_dec_6_g), .A(dec_disp_dec_6_a));
  DD_32b dd_32b_1 (
    .A(in_3), .P4_7(dd_32b_1_p4_7), .P8_11(dd_32b_1_p8_11), .P12_15(dd_32b_1_p12_15),
    .P16_19(dd_32b_1_p16_19), .P20_23(dd_32b_1_p20_23), .P24_27(dd_32b_1_p24_27), .P28_31(dd_32b_1_p28_31),
    .P32_35(dd_32b_1_p32_35), .P36_39(dd_32b_1_p36_39), .P0_3(dd_32b_1_p0_3));
  _7_Segment_Display #(.decimalPoint("false")) u_7_segment_display_7 (
    .g(dec_disp_dec_7_g), .f(dec_disp_dec_7_f), .a(dec_disp_dec_7_a), .b(dec_disp_dec_7_b),
    .e(dec_disp_dec_7_e), .d(dec_disp_dec_7_d), .c(dec_disp_dec_7_c));
  _7_Segment_Display #(.decimalPoint("false")) u_7_segment_display_8 (
    .g(dec_disp_dec_8_g), .f(dec_disp_dec_8_f), .a(dec_disp_dec_8_a), .b(dec_disp_dec_8_b),
    .e(dec_disp_dec_8_e), .d(dec_disp_dec_8_d), .c(dec_disp_dec_8_c));
  DEC_DISP_DEC dec_disp_dec_7 (
    .En(t_box_2_s), .X(dd_16b_1_p8_11), .B(dec_disp_dec_7_b), .C(dec_disp_dec_7_c), .D(dec_disp_dec_7_d),
    .E(dec_disp_dec_7_e), .F(dec_disp_dec_7_f), .G(dec_disp_dec_7_g), .A(dec_disp_dec_7_a));
  DEC_DISP_DEC dec_disp_dec_8 (
    .En(t_box_2_s), .X(dd_16b_1_p4_7), .B(dec_disp_dec_8_b), .C(dec_disp_dec_8_c), .D(dec_disp_dec_8_d),
    .E(dec_disp_dec_8_e), .F(dec_disp_dec_8_f), .G(dec_disp_dec_8_g), .A(dec_disp_dec_8_a));
  _7_Segment_Display #(.decimalPoint("false")) u_7_segment_display_9 (
    .g(dec_disp_dec_9_g), .f(dec_disp_dec_9_f), .a(dec_disp_dec_9_a), .b(dec_disp_dec_9_b),
    .e(dec_disp_dec_9_e), .d(dec_disp_dec_9_d), .c(dec_disp_dec_9_c));
  _7_Segment_Display #(.decimalPoint("false")) u_7_segment_display_10 (
    .g(dec_disp_dec_10_g), .f(dec_disp_dec_10_f), .a(dec_disp_dec_10_a), .b(dec_disp_dec_10_b),
    .e(dec_disp_dec_10_e), .d(dec_disp_dec_10_d), .c(dec_disp_dec_10_c));
  DEC_DISP_DEC dec_disp_dec_9 (
    .En(t_box_3_s), .X(dd_32b_1_p32_35), .B(dec_disp_dec_9_b), .C(dec_disp_dec_9_c), .D(dec_disp_dec_9_d),
    .E(dec_disp_dec_9_e), .F(dec_disp_dec_9_f), .G(dec_disp_dec_9_g), .A(dec_disp_dec_9_a));
  DEC_DISP_DEC dec_disp_dec_10 (
    .En(t_box_3_s), .X(dd_32b_1_p28_31), .B(dec_disp_dec_10_b), .C(dec_disp_dec_10_c), .D(dec_disp_dec_10_d),
    .E(dec_disp_dec_10_e), .F(dec_disp_dec_10_f), .G(dec_disp_dec_10_g), .A(dec_disp_dec_10_a));
  _7_Segment_Display #(.decimalPoint("false")) u_7_segment_display_11 (
    .g(dec_disp_dec_11_g), .f(dec_disp_dec_11_f), .a(dec_disp_dec_11_a), .b(dec_disp_dec_11_b),
    .e(dec_disp_dec_11_e), .d(dec_disp_dec_11_d), .c(dec_disp_dec_11_c));
  DEC_DISP_DEC dec_disp_dec_11 (
    .En(t_box_2_s), .X(dd_16b_1_p0_3), .B(dec_disp_dec_11_b), .C(dec_disp_dec_11_c), .D(dec_disp_dec_11_d),
    .E(dec_disp_dec_11_e), .F(dec_disp_dec_11_f), .G(dec_disp_dec_11_g), .A(dec_disp_dec_11_a));
  _7_Segment_Display #(.decimalPoint("false")) u_7_segment_display_12 (
    .g(dec_disp_dec_12_g), .f(dec_disp_dec_12_f), .a(dec_disp_dec_12_a), .b(dec_disp_dec_12_b),
    .e(dec_disp_dec_12_e), .d(dec_disp_dec_12_d), .c(dec_disp_dec_12_c));
  _7_Segment_Display #(.decimalPoint("false")) u_7_segment_display_13 (
    .g(dec_disp_dec_13_g), .f(dec_disp_dec_13_f), .a(dec_disp_dec_13_a), .b(dec_disp_dec_13_b),
    .e(dec_disp_dec_13_e), .d(dec_disp_dec_13_d), .c(dec_disp_dec_13_c));
  DEC_DISP_DEC dec_disp_dec_12 (
    .En(t_box_3_s), .X(dd_32b_1_p24_27), .B(dec_disp_dec_12_b), .C(dec_disp_dec_12_c), .D(dec_disp_dec_12_d),
    .E(dec_disp_dec_12_e), .F(dec_disp_dec_12_f), .G(dec_disp_dec_12_g), .A(dec_disp_dec_12_a));
  DEC_DISP_DEC dec_disp_dec_13 (
    .En(t_box_3_s), .X(dd_32b_1_p20_23), .B(dec_disp_dec_13_b), .C(dec_disp_dec_13_c), .D(dec_disp_dec_13_d),
    .E(dec_disp_dec_13_e), .F(dec_disp_dec_13_f), .G(dec_disp_dec_13_g), .A(dec_disp_dec_13_a));
  _7_Segment_Display #(.decimalPoint("false")) u_7_segment_display_14 (
    .g(dec_disp_dec_14_g), .f(dec_disp_dec_14_f), .a(dec_disp_dec_14_a), .b(dec_disp_dec_14_b),
    .e(dec_disp_dec_14_e), .d(dec_disp_dec_14_d), .c(dec_disp_dec_14_c));
  _7_Segment_Display #(.decimalPoint("false")) u_7_segment_display_15 (
    .g(dec_disp_dec_15_g), .f(dec_disp_dec_15_f), .a(dec_disp_dec_15_a), .b(dec_disp_dec_15_b),
    .e(dec_disp_dec_15_e), .d(dec_disp_dec_15_d), .c(dec_disp_dec_15_c));
  DEC_DISP_DEC dec_disp_dec_14 (
    .En(t_box_3_s), .X(dd_32b_1_p16_19), .B(dec_disp_dec_14_b), .C(dec_disp_dec_14_c), .D(dec_disp_dec_14_d),
    .E(dec_disp_dec_14_e), .F(dec_disp_dec_14_f), .G(dec_disp_dec_14_g), .A(dec_disp_dec_14_a));
  DEC_DISP_DEC dec_disp_dec_15 (
    .En(t_box_3_s), .X(dd_32b_1_p12_15), .B(dec_disp_dec_15_b), .C(dec_disp_dec_15_c), .D(dec_disp_dec_15_d),
    .E(dec_disp_dec_15_e), .F(dec_disp_dec_15_f), .G(dec_disp_dec_15_g), .A(dec_disp_dec_15_a));
  _7_Segment_Display #(.decimalPoint("false")) u_7_segment_display_16 (
    .g(dec_disp_dec_16_g), .f(dec_disp_dec_16_f), .a(dec_disp_dec_16_a), .b(dec_disp_dec_16_b),
    .e(dec_disp_dec_16_e), .d(dec_disp_dec_16_d), .c(dec_disp_dec_16_c));
  _7_Segment_Display #(.decimalPoint("false")) u_7_segment_display_17 (
    .g(dec_disp_dec_17_g), .f(dec_disp_dec_17_f), .a(dec_disp_dec_17_a), .b(dec_disp_dec_17_b),
    .e(dec_disp_dec_17_e), .d(dec_disp_dec_17_d), .c(dec_disp_dec_17_c));
  DEC_DISP_DEC dec_disp_dec_16 (
    .En(t_box_3_s), .X(dd_32b_1_p8_11), .B(dec_disp_dec_16_b), .C(dec_disp_dec_16_c), .D(dec_disp_dec_16_d),
    .E(dec_disp_dec_16_e), .F(dec_disp_dec_16_f), .G(dec_disp_dec_16_g), .A(dec_disp_dec_16_a));
  DEC_DISP_DEC dec_disp_dec_17 (
    .En(t_box_3_s), .X(dd_32b_1_p4_7), .B(dec_disp_dec_17_b), .C(dec_disp_dec_17_c), .D(dec_disp_dec_17_d),
    .E(dec_disp_dec_17_e), .F(dec_disp_dec_17_f), .G(dec_disp_dec_17_g), .A(dec_disp_dec_17_a));
  _7_Segment_Display #(.decimalPoint("false")) u_7_segment_display_18 (
    .g(dec_disp_dec_18_g), .f(dec_disp_dec_18_f), .a(dec_disp_dec_18_a), .b(dec_disp_dec_18_b),
    .e(dec_disp_dec_18_e), .d(dec_disp_dec_18_d), .c(dec_disp_dec_18_c));
  DEC_DISP_DEC dec_disp_dec_18 (
    .En(t_box_3_s), .X(dd_32b_1_p0_3), .B(dec_disp_dec_18_b), .C(dec_disp_dec_18_c), .D(dec_disp_dec_18_d),
    .E(dec_disp_dec_18_e), .F(dec_disp_dec_18_f), .G(dec_disp_dec_18_g), .A(dec_disp_dec_18_a));
endmodule

module SHIFT_ADD (
  input  A0,
  input  A1,
  input  A2,
  input  A3,
  output S0,
  output S1,
  output S2,
  output S3
);

  PLA #(.in_width(4), .out_width(4), .\table ("0000 0000 # 0\n0001 0001 # 1\n0010 0010 # 2\n0011 0011 # 3\n0100 0100 # 4\n0101 1000 # 5\n0110 1001 # 6\n0111 1010 # 7\n1000 1011 # 8\n1001 1100 # 9")) pla_1 (
    .in({A3, A2, A1, A0}), .out({S3, S2, S1, S0}));
endmodule

module DD_8b (
  input  [7:0] A,
  output [3:0] P0_3,
  output [3:0] P4_7,
  output [1:0] P8_9
);

  wire shift_add_1_s0, shift_add_1_s1, shift_add_1_s2, shift_add_1_s3, shift_add_2_s0, shift_add_2_s1,
       shift_add_2_s2, shift_add_2_s3, shift_add_3_s0, shift_add_3_s1, shift_add_3_s2, shift_add_3_s3,
       shift_add_4_s0, shift_add_4_s1, shift_add_4_s2, shift_add_4_s3, shift_add_5_s0, shift_add_5_s1,
       shift_add_5_s2;

  SHIFT_ADD shift_add_1 (
    .A2(A[7]), .A3(1'b0), .A0(A[5]), .A1(A[6]), .S2(shift_add_1_s2), .S3(shift_add_1_s3),
    .S0(shift_add_1_s0), .S1(shift_add_1_s1));
  SHIFT_ADD shift_add_2 (
    .A2(shift_add_1_s1), .A3(shift_add_1_s2), .A0(A[4]), .A1(shift_add_1_s0), .S2(shift_add_2_s2),
    .S3(shift_add_2_s3), .S0(shift_add_2_s0), .S1(shift_add_2_s1));
  SHIFT_ADD shift_add_3 (
    .A2(shift_add_4_s1), .A3(shift_add_4_s2), .A0(A[2]), .A1(shift_add_4_s0), .S2(shift_add_3_s2),
    .S3(shift_add_3_s3), .S0(shift_add_3_s0), .S1(shift_add_3_s1));
  SHIFT_ADD shift_add_4 (
    .A2(shift_add_2_s1), .A3(shift_add_2_s2), .A0(A[3]), .A1(shift_add_2_s0), .S2(shift_add_4_s2),
    .S3(shift_add_4_s3), .S0(shift_add_4_s0), .S1(shift_add_4_s1));
  SHIFT_ADD shift_add_5 (
    .A2(shift_add_1_s3), .A3(1'b0), .A0(shift_add_4_s3), .A1(shift_add_2_s3), .S2(shift_add_5_s2),
    .S3(P8_9[1]), .S0(shift_add_5_s0), .S1(shift_add_5_s1));
  SHIFT_ADD shift_add_6 (
    .A2(shift_add_3_s1), .A3(shift_add_3_s2), .A0(A[1]), .A1(shift_add_3_s0), .S2(P0_3[3]), .S3(P4_7[0]),
    .S0(P0_3[1]), .S1(P0_3[2]));
  SHIFT_ADD shift_add_7 (
    .A2(shift_add_5_s1), .A3(shift_add_5_s2), .A0(shift_add_3_s3), .A1(shift_add_5_s0), .S2(P4_7[3]),
    .S3(P8_9[0]), .S0(P4_7[1]), .S1(P4_7[2]));

  assign P0_3[0] = A[0];
endmodule

module DD_16b (
  input  [15:0] A,
  output [3:0] P0_3,
  output [3:0] P4_7,
  output [3:0] P8_11,
  output [3:0] P12_15,
  output [3:0] P16_19
);

  wire shift_add_1_s0, shift_add_1_s1, shift_add_1_s2, shift_add_1_s3, shift_add_2_s0, shift_add_2_s1,
       shift_add_2_s2, shift_add_2_s3, shift_add_3_s0, shift_add_3_s1, shift_add_3_s2, shift_add_3_s3,
       shift_add_4_s0, shift_add_4_s1, shift_add_4_s2, shift_add_4_s3, shift_add_5_s0, shift_add_5_s1,
       shift_add_5_s2, shift_add_5_s3, shift_add_6_s0, shift_add_6_s1, shift_add_6_s2, shift_add_6_s3,
       shift_add_7_s0, shift_add_7_s1, shift_add_7_s2, shift_add_7_s3, shift_add_8_s0, shift_add_8_s1,
       shift_add_8_s2, shift_add_8_s3, shift_add_9_s0, shift_add_9_s1, shift_add_9_s2, shift_add_9_s3,
       shift_add_10_s0, shift_add_10_s1, shift_add_10_s2, shift_add_10_s3, shift_add_11_s0, shift_add_11_s1,
       shift_add_11_s2, shift_add_11_s3, shift_add_12_s0, shift_add_12_s1, shift_add_12_s2, shift_add_12_s3,
       shift_add_13_s0, shift_add_13_s1, shift_add_13_s2, shift_add_13_s3, shift_add_14_s0, shift_add_14_s1,
       shift_add_14_s2, shift_add_14_s3, shift_add_15_s0, shift_add_15_s1, shift_add_15_s2, shift_add_15_s3,
       shift_add_16_s0, shift_add_16_s1, shift_add_16_s2, shift_add_16_s3, shift_add_17_s0, shift_add_17_s1,
       shift_add_17_s2, shift_add_17_s3, shift_add_18_s0, shift_add_18_s1, shift_add_18_s2, shift_add_18_s3,
       shift_add_19_s0, shift_add_19_s1, shift_add_19_s2, shift_add_19_s3, shift_add_20_s0, shift_add_20_s1,
       shift_add_20_s2, shift_add_20_s3, shift_add_21_s0, shift_add_21_s1, shift_add_21_s2, shift_add_21_s3,
       shift_add_22_s0, shift_add_22_s1, shift_add_22_s2, shift_add_23_s0, shift_add_23_s1, shift_add_23_s2,
       shift_add_23_s3, shift_add_24_s0, shift_add_24_s1, shift_add_24_s2, shift_add_24_s3, shift_add_25_s0,
       shift_add_25_s1, shift_add_25_s2, shift_add_25_s3, shift_add_26_s0, shift_add_26_s1, shift_add_26_s2,
       shift_add_28_s0, shift_add_28_s1, shift_add_28_s2, shift_add_28_s3, shift_add_30_s0, shift_add_30_s1,
       shift_add_30_s2, shift_add_30_s3, shift_add_32_s0, shift_add_32_s1, shift_add_32_s2, shift_add_32_s3,
       shift_add_34_s0, shift_add_34_s1, shift_add_34_s2;

  SHIFT_ADD shift_add_1 (
    .A2(A[15]), .A3(1'b0), .A0(A[13]), .A1(A[14]), .S2(shift_add_1_s2), .S3(shift_add_1_s3),
    .S0(shift_add_1_s0), .S1(shift_add_1_s1));
  SHIFT_ADD shift_add_2 (
    .A2(shift_add_1_s1), .A3(shift_add_1_s2), .A0(A[12]), .A1(shift_add_1_s0), .S2(shift_add_2_s2),
    .S3(shift_add_2_s3), .S0(shift_add_2_s0), .S1(shift_add_2_s1));
  SHIFT_ADD shift_add_3 (
    .A2(shift_add_2_s1), .A3(shift_add_2_s2), .A0(A[11]), .A1(shift_add_2_s0), .S2(shift_add_3_s2),
    .S3(shift_add_3_s3), .S0(shift_add_3_s0), .S1(shift_add_3_s1));
  SHIFT_ADD shift_add_4 (
    .A2(shift_add_5_s1), .A3(shift_add_5_s2), .A0(A[9]), .A1(shift_add_5_s0), .S2(shift_add_4_s2),
    .S3(shift_add_4_s3), .S0(shift_add_4_s0), .S1(shift_add_4_s1));
  SHIFT_ADD shift_add_5 (
    .A2(shift_add_3_s1), .A3(shift_add_3_s2), .A0(A[10]), .A1(shift_add_3_s0), .S2(shift_add_5_s2),
    .S3(shift_add_5_s3), .S0(shift_add_5_s0), .S1(shift_add_5_s1));
  SHIFT_ADD shift_add_6 (
    .A2(shift_add_7_s1), .A3(shift_add_7_s2), .A0(shift_add_5_s3), .A1(shift_add_7_s0), .S2(shift_add_6_s2),
    .S3(shift_add_6_s3), .S0(shift_add_6_s0), .S1(shift_add_6_s1));
  SHIFT_ADD shift_add_7 (
    .A2(shift_add_1_s3), .A3(1'b0), .A0(shift_add_3_s3), .A1(shift_add_2_s3), .S2(shift_add_7_s2),
    .S3(shift_add_7_s3), .S0(shift_add_7_s0), .S1(shift_add_7_s1));
  SHIFT_ADD shift_add_8 (
    .A2(shift_add_4_s1), .A3(shift_add_4_s2), .A0(A[8]), .A1(shift_add_4_s0), .S2(shift_add_8_s2),
    .S3(shift_add_8_s3), .S0(shift_add_8_s0), .S1(shift_add_8_s1));
  SHIFT_ADD shift_add_9 (
    .A2(shift_add_6_s1), .A3(shift_add_6_s2), .A0(shift_add_4_s3), .A1(shift_add_6_s0), .S2(shift_add_9_s2),
    .S3(shift_add_9_s3), .S0(shift_add_9_s0), .S1(shift_add_9_s1));
  SHIFT_ADD shift_add_10 (
    .A2(shift_add_8_s1), .A3(shift_add_8_s2), .A0(A[7]), .A1(shift_add_8_s0), .S2(shift_add_10_s2),
    .S3(shift_add_10_s3), .S0(shift_add_10_s0), .S1(shift_add_10_s1));
  SHIFT_ADD shift_add_11 (
    .A2(shift_add_9_s1), .A3(shift_add_9_s2), .A0(shift_add_8_s3), .A1(shift_add_9_s0), .S2(shift_add_11_s2),
    .S3(shift_add_11_s3), .S0(shift_add_11_s0), .S1(shift_add_11_s1));
  SHIFT_ADD shift_add_12 (
    .A2(shift_add_7_s3), .A3(1'b0), .A0(shift_add_9_s3), .A1(shift_add_6_s3), .S2(shift_add_12_s2),
    .S3(shift_add_12_s3), .S0(shift_add_12_s0), .S1(shift_add_12_s1));
  SHIFT_ADD shift_add_13 (
    .A2(shift_add_14_s1), .A3(shift_add_14_s2), .A0(A[5]), .A1(shift_add_14_s0), .S2(shift_add_13_s2),
    .S3(shift_add_13_s3), .S0(shift_add_13_s0), .S1(shift_add_13_s1));
  SHIFT_ADD shift_add_14 (
    .A2(shift_add_10_s1), .A3(shift_add_10_s2), .A0(A[6]), .A1(shift_add_10_s0), .S2(shift_add_14_s2),
    .S3(shift_add_14_s3), .S0(shift_add_14_s0), .S1(shift_add_14_s1));
  SHIFT_ADD shift_add_15 (
    .A2(shift_add_16_s1), .A3(shift_add_16_s2), .A0(shift_add_14_s3), .A1(shift_add_16_s0),
    .S2(shift_add_15_s2), .S3(shift_add_15_s3), .S0(shift_add_15_s0), .S1(shift_add_15_s1));
  SHIFT_ADD shift_add_16 (
    .A2(shift_add_11_s1), .A3(shift_add_11_s2), .A0(shift_add_10_s3), .A1(shift_add_11_s0),
    .S2(shift_add_16_s2), .S3(shift_add_16_s3), .S0(shift_add_16_s0), .S1(shift_add_16_s1));
  SHIFT_ADD shift_add_17 (
    .A2(shift_add_18_s1), .A3(shift_add_18_s2), .A0(shift_add_16_s3), .A1(shift_add_18_s0),
    .S2(shift_add_17_s2), .S3(shift_add_17_s3), .S0(shift_add_17_s0), .S1(shift_add_17_s1));
  SHIFT_ADD shift_add_18 (
    .A2(shift_add_12_s1), .A3(shift_add_12_s2), .A0(shift_add_11_s3), .A1(shift_add_12_s0),
    .S2(shift_add_18_s2), .S3(shift_add_18_s3), .S0(shift_add_18_s0), .S1(shift_add_18_s1));
  SHIFT_ADD shift_add_19 (
    .A2(shift_add_13_s1), .A3(shift_add_13_s2), .A0(A[4]), .A1(shift_add_13_s0), .S2(shift_add_19_s2),
    .S3(shift_add_19_s3), .S0(shift_add_19_s0), .S1(shift_add_19_s1));
  SHIFT_ADD shift_add_20 (
    .A2(shift_add_15_s1), .A3(shift_add_15_s2), .A0(shift_add_13_s3), .A1(shift_add_15_s0),
    .S2(shift_add_20_s2), .S3(shift_add_20_s3), .S0(shift_add_20_s0), .S1(shift_add_20_s1));
  SHIFT_ADD shift_add_21 (
    .A2(shift_add_17_s1), .A3(shift_add_17_s2), .A0(shift_add_15_s3), .A1(shift_add_17_s0),
    .S2(shift_add_21_s2), .S3(shift_add_21_s3), .S0(shift_add_21_s0), .S1(shift_add_21_s1));
  SHIFT_ADD shift_add_22 (
    .A2(shift_add_12_s3), .A3(1'b0), .A0(shift_add_17_s3), .A1(shift_add_18_s3), .S2(shift_add_22_s2),
    .S3(P16_19[3]), .S0(shift_add_22_s0), .S1(shift_add_22_s1));
  SHIFT_ADD shift_add_23 (
    .A2(shift_add_19_s1), .A3(shift_add_19_s2), .A0(A[3]), .A1(shift_add_19_s0), .S2(shift_add_23_s2),
    .S3(shift_add_23_s3), .S0(shift_add_23_s0), .S1(shift_add_23_s1));
  SHIFT_ADD shift_add_24 (
    .A2(shift_add_20_s1), .A3(shift_add_20_s2), .A0(shift_add_19_s3), .A1(shift_add_20_s0),
    .S2(shift_add_24_s2), .S3(shift_add_24_s3), .S0(shift_add_24_s0), .S1(shift_add_24_s1));
  SHIFT_ADD shift_add_25 (
    .A2(shift_add_21_s1), .A3(shift_add_21_s2), .A0(shift_add_20_s3), .A1(shift_add_21_s0),
    .S2(shift_add_25_s2), .S3(shift_add_25_s3), .S0(shift_add_25_s0), .S1(shift_add_25_s1));
  SHIFT_ADD shift_add_26 (
    .A2(shift_add_22_s1), .A3(shift_add_22_s2), .A0(shift_add_21_s3), .A1(shift_add_22_s0),
    .S2(shift_add_26_s2), .S3(P16_19[2]), .S0(shift_add_26_s0), .S1(shift_add_26_s1));
  SHIFT_ADD shift_add_27 (
    .A2(shift_add_28_s1), .A3(shift_add_28_s2), .A0(A[1]), .A1(shift_add_28_s0), .S2(P0_3[3]), .S3(P4_7[0]),
    .S0(P0_3[1]), .S1(P0_3[2]));
  SHIFT_ADD shift_add_28 (
    .A2(shift_add_23_s1), .A3(shift_add_23_s2), .A0(A[2]), .A1(shift_add_23_s0), .S2(shift_add_28_s2),
    .S3(shift_add_28_s3), .S0(shift_add_28_s0), .S1(shift_add_28_s1));
  SHIFT_ADD shift_add_29 (
    .A2(shift_add_30_s1), .A3(shift_add_30_s2), .A0(shift_add_28_s3), .A1(shift_add_30_s0), .S2(P4_7[3]),
    .S3(P8_11[0]), .S0(P4_7[1]), .S1(P4_7[2]));
  SHIFT_ADD shift_add_30 (
    .A2(shift_add_24_s1), .A3(shift_add_24_s2), .A0(shift_add_23_s3), .A1(shift_add_24_s0),
    .S2(shift_add_30_s2), .S3(shift_add_30_s3), .S0(shift_add_30_s0), .S1(shift_add_30_s1));
  SHIFT_ADD shift_add_31 (
    .A2(shift_add_32_s1), .A3(shift_add_32_s2), .A0(shift_add_30_s3), .A1(shift_add_32_s0), .S2(P8_11[3]),
    .S3(P12_15[0]), .S0(P8_11[1]), .S1(P8_11[2]));
  SHIFT_ADD shift_add_32 (
    .A2(shift_add_25_s1), .A3(shift_add_25_s2), .A0(shift_add_24_s3), .A1(shift_add_25_s0),
    .S2(shift_add_32_s2), .S3(shift_add_32_s3), .S0(shift_add_32_s0), .S1(shift_add_32_s1));
  SHIFT_ADD shift_add_33 (
    .A2(shift_add_34_s1), .A3(shift_add_34_s2), .A0(shift_add_32_s3), .A1(shift_add_34_s0), .S2(P12_15[3]),
    .S3(P16_19[0]), .S0(P12_15[1]), .S1(P12_15[2]));
  SHIFT_ADD shift_add_34 (
    .A2(shift_add_26_s1), .A3(shift_add_26_s2), .A0(shift_add_25_s3), .A1(shift_add_26_s0),
    .S2(shift_add_34_s2), .S3(P16_19[1]), .S0(shift_add_34_s0), .S1(shift_add_34_s1));

  assign P0_3[0] = A[0];
endmodule

module DD_32b (
  input  [31:0] A,
  output [3:0] P0_3,
  output [3:0] P4_7,
  output [3:0] P8_11,
  output [3:0] P12_15,
  output [3:0] P16_19,
  output [3:0] P20_23,
  output [3:0] P24_27,
  output [3:0] P28_31,
  output [3:0] P32_35,
  output [3:0] P36_39
);

  wire shift_add_1_s0, shift_add_1_s1, shift_add_1_s2, shift_add_1_s3, shift_add_2_s0, shift_add_2_s1,
       shift_add_2_s2, shift_add_2_s3, shift_add_3_s0, shift_add_3_s1, shift_add_3_s2, shift_add_3_s3,
       shift_add_4_s0, shift_add_4_s1, shift_add_4_s2, shift_add_4_s3, shift_add_5_s0, shift_add_5_s1,
       shift_add_5_s2, shift_add_5_s3, shift_add_6_s0, shift_add_6_s1, shift_add_6_s2, shift_add_6_s3,
       shift_add_7_s0, shift_add_7_s1, shift_add_7_s2, shift_add_7_s3, shift_add_8_s0, shift_add_8_s1,
       shift_add_8_s2, shift_add_8_s3, shift_add_9_s0, shift_add_9_s1, shift_add_9_s2, shift_add_9_s3,
       shift_add_10_s0, shift_add_10_s1, shift_add_10_s2, shift_add_10_s3, shift_add_11_s0, shift_add_11_s1,
       shift_add_11_s2, shift_add_11_s3, shift_add_12_s0, shift_add_12_s1, shift_add_12_s2, shift_add_12_s3,
       shift_add_13_s0, shift_add_13_s1, shift_add_13_s2, shift_add_13_s3, shift_add_14_s0, shift_add_14_s1,
       shift_add_14_s2, shift_add_14_s3, shift_add_15_s0, shift_add_15_s1, shift_add_15_s2, shift_add_15_s3,
       shift_add_16_s0, shift_add_16_s1, shift_add_16_s2, shift_add_16_s3, shift_add_17_s0, shift_add_17_s1,
       shift_add_17_s2, shift_add_17_s3, shift_add_18_s0, shift_add_18_s1, shift_add_18_s2, shift_add_18_s3,
       shift_add_19_s0, shift_add_19_s1, shift_add_19_s2, shift_add_19_s3, shift_add_20_s0, shift_add_20_s1,
       shift_add_20_s2, shift_add_20_s3, shift_add_21_s0, shift_add_21_s1, shift_add_21_s2, shift_add_21_s3,
       shift_add_22_s0, shift_add_22_s1, shift_add_22_s2, shift_add_22_s3, shift_add_23_s0, shift_add_23_s1,
       shift_add_23_s2, shift_add_23_s3, shift_add_24_s0, shift_add_24_s1, shift_add_24_s2, shift_add_24_s3,
       shift_add_25_s0, shift_add_25_s1, shift_add_25_s2, shift_add_25_s3, shift_add_26_s0, shift_add_26_s1,
       shift_add_26_s2, shift_add_26_s3, shift_add_27_s0, shift_add_27_s1, shift_add_27_s2, shift_add_27_s3,
       shift_add_28_s0, shift_add_28_s1, shift_add_28_s2, shift_add_28_s3, shift_add_29_s0, shift_add_29_s1,
       shift_add_29_s2, shift_add_29_s3, shift_add_30_s0, shift_add_30_s1, shift_add_30_s2, shift_add_30_s3,
       shift_add_31_s0, shift_add_31_s1, shift_add_31_s2, shift_add_31_s3, shift_add_32_s0, shift_add_32_s1,
       shift_add_32_s2, shift_add_32_s3, shift_add_33_s0, shift_add_33_s1, shift_add_33_s2, shift_add_33_s3,
       shift_add_34_s0, shift_add_34_s1, shift_add_34_s2, shift_add_34_s3, shift_add_35_s0, shift_add_35_s1,
       shift_add_35_s2, shift_add_35_s3, shift_add_36_s0, shift_add_36_s1, shift_add_36_s2, shift_add_36_s3,
       shift_add_37_s0, shift_add_37_s1, shift_add_37_s2, shift_add_37_s3, shift_add_38_s0, shift_add_38_s1,
       shift_add_38_s2, shift_add_38_s3, shift_add_39_s0, shift_add_39_s1, shift_add_39_s2, shift_add_39_s3,
       shift_add_40_s0, shift_add_40_s1, shift_add_40_s2, shift_add_40_s3, shift_add_41_s0, shift_add_41_s1,
       shift_add_41_s2, shift_add_41_s3, shift_add_42_s0, shift_add_42_s1, shift_add_42_s2, shift_add_42_s3,
       shift_add_43_s0, shift_add_43_s1, shift_add_43_s2, shift_add_43_s3, shift_add_44_s0, shift_add_44_s1,
       shift_add_44_s2, shift_add_44_s3, shift_add_45_s0, shift_add_45_s1, shift_add_45_s2, shift_add_45_s3,
       shift_add_46_s0, shift_add_46_s1, shift_add_46_s2, shift_add_46_s3, shift_add_47_s0, shift_add_47_s1,
       shift_add_47_s2, shift_add_47_s3, shift_add_48_s0, shift_add_48_s1, shift_add_48_s2, shift_add_48_s3,
       shift_add_49_s0, shift_add_49_s1, shift_add_49_s2, shift_add_49_s3, shift_add_50_s0, shift_add_50_s1,
       shift_add_50_s2, shift_add_50_s3, shift_add_51_s0, shift_add_51_s1, shift_add_51_s2, shift_add_51_s3,
       shift_add_52_s0, shift_add_52_s1, shift_add_52_s2, shift_add_52_s3, shift_add_53_s0, shift_add_53_s1,
       shift_add_53_s2, shift_add_53_s3, shift_add_54_s0, shift_add_54_s1, shift_add_54_s2, shift_add_54_s3,
       shift_add_55_s0, shift_add_55_s1, shift_add_55_s2, shift_add_55_s3, shift_add_56_s0, shift_add_56_s1,
       shift_add_56_s2, shift_add_56_s3, shift_add_57_s0, shift_add_57_s1, shift_add_57_s2, shift_add_57_s3,
       shift_add_58_s0, shift_add_58_s1, shift_add_58_s2, shift_add_58_s3, shift_add_59_s0, shift_add_59_s1,
       shift_add_59_s2, shift_add_59_s3, shift_add_60_s0, shift_add_60_s1, shift_add_60_s2, shift_add_60_s3,
       shift_add_61_s0, shift_add_61_s1, shift_add_61_s2, shift_add_61_s3, shift_add_62_s0, shift_add_62_s1,
       shift_add_62_s2, shift_add_62_s3, shift_add_63_s0, shift_add_63_s1, shift_add_63_s2, shift_add_63_s3,
       shift_add_64_s0, shift_add_64_s1, shift_add_64_s2, shift_add_64_s3, shift_add_65_s0, shift_add_65_s1,
       shift_add_65_s2, shift_add_65_s3, shift_add_66_s0, shift_add_66_s1, shift_add_66_s2, shift_add_66_s3,
       shift_add_67_s0, shift_add_67_s1, shift_add_67_s2, shift_add_67_s3, shift_add_68_s0, shift_add_68_s1,
       shift_add_68_s2, shift_add_68_s3, shift_add_69_s0, shift_add_69_s1, shift_add_69_s2, shift_add_69_s3,
       shift_add_70_s0, shift_add_70_s1, shift_add_70_s2, shift_add_70_s3, shift_add_71_s0, shift_add_71_s1,
       shift_add_71_s2, shift_add_71_s3, shift_add_72_s0, shift_add_72_s1, shift_add_72_s2, shift_add_72_s3,
       shift_add_73_s0, shift_add_73_s1, shift_add_73_s2, shift_add_73_s3, shift_add_74_s0, shift_add_74_s1,
       shift_add_74_s2, shift_add_74_s3, shift_add_75_s0, shift_add_75_s1, shift_add_75_s2, shift_add_75_s3,
       shift_add_76_s0, shift_add_76_s1, shift_add_76_s2, shift_add_76_s3, shift_add_77_s0, shift_add_77_s1,
       shift_add_77_s2, shift_add_77_s3, shift_add_78_s0, shift_add_78_s1, shift_add_78_s2, shift_add_78_s3,
       shift_add_79_s0, shift_add_79_s1, shift_add_79_s2, shift_add_79_s3, shift_add_80_s0, shift_add_80_s1,
       shift_add_80_s2, shift_add_80_s3, shift_add_81_s0, shift_add_81_s1, shift_add_81_s2, shift_add_81_s3,
       shift_add_82_s0, shift_add_82_s1, shift_add_82_s2, shift_add_82_s3, shift_add_83_s0, shift_add_83_s1,
       shift_add_83_s2, shift_add_83_s3, shift_add_84_s0, shift_add_84_s1, shift_add_84_s2, shift_add_84_s3,
       shift_add_85_s0, shift_add_85_s1, shift_add_85_s2, shift_add_85_s3, shift_add_86_s0, shift_add_86_s1,
       shift_add_86_s2, shift_add_86_s3, shift_add_87_s0, shift_add_87_s1, shift_add_87_s2, shift_add_87_s3,
       shift_add_88_s0, shift_add_88_s1, shift_add_88_s2, shift_add_88_s3, shift_add_89_s0, shift_add_89_s1,
       shift_add_89_s2, shift_add_89_s3, shift_add_90_s0, shift_add_90_s1, shift_add_90_s2, shift_add_90_s3,
       shift_add_91_s0, shift_add_91_s1, shift_add_91_s2, shift_add_91_s3, shift_add_92_s0, shift_add_92_s1,
       shift_add_92_s2, shift_add_92_s3, shift_add_93_s0, shift_add_93_s1, shift_add_93_s2, shift_add_93_s3,
       shift_add_94_s0, shift_add_94_s1, shift_add_94_s2, shift_add_94_s3, shift_add_95_s0, shift_add_95_s1,
       shift_add_95_s2, shift_add_95_s3, shift_add_96_s0, shift_add_96_s1, shift_add_96_s2, shift_add_96_s3,
       shift_add_97_s0, shift_add_97_s1, shift_add_97_s2, shift_add_97_s3, shift_add_98_s0, shift_add_98_s1,
       shift_add_98_s2, shift_add_98_s3, shift_add_99_s0, shift_add_99_s1, shift_add_99_s2, shift_add_99_s3,
       shift_add_100_s0, shift_add_100_s1, shift_add_100_s2, shift_add_100_s3, shift_add_101_s0,
       shift_add_101_s1, shift_add_101_s2, shift_add_101_s3, shift_add_102_s0, shift_add_102_s1,
       shift_add_102_s2, shift_add_102_s3, shift_add_103_s0, shift_add_103_s1, shift_add_103_s2,
       shift_add_103_s3, shift_add_104_s0, shift_add_104_s1, shift_add_104_s2, shift_add_104_s3,
       shift_add_105_s0, shift_add_105_s1, shift_add_105_s2, shift_add_105_s3, shift_add_106_s0,
       shift_add_106_s1, shift_add_106_s2, shift_add_106_s3, shift_add_107_s0, shift_add_107_s1,
       shift_add_107_s2, shift_add_107_s3, shift_add_108_s0, shift_add_108_s1, shift_add_108_s2,
       shift_add_108_s3, shift_add_109_s0, shift_add_109_s1, shift_add_109_s2, shift_add_109_s3,
       shift_add_110_s0, shift_add_110_s1, shift_add_110_s2, shift_add_110_s3, shift_add_111_s0,
       shift_add_111_s1, shift_add_111_s2, shift_add_111_s3, shift_add_112_s0, shift_add_112_s1,
       shift_add_112_s2, shift_add_112_s3, shift_add_113_s0, shift_add_113_s1, shift_add_113_s2,
       shift_add_113_s3, shift_add_114_s0, shift_add_114_s1, shift_add_114_s2, shift_add_114_s3,
       shift_add_115_s0, shift_add_115_s1, shift_add_115_s2, shift_add_115_s3, shift_add_116_s0,
       shift_add_116_s1, shift_add_116_s2, shift_add_116_s3, shift_add_117_s0, shift_add_117_s1,
       shift_add_117_s2, shift_add_117_s3, shift_add_118_s0, shift_add_118_s1, shift_add_118_s2,
       shift_add_118_s3, shift_add_119_s0, shift_add_119_s1, shift_add_119_s2, shift_add_119_s3,
       shift_add_120_s0, shift_add_120_s1, shift_add_120_s2, shift_add_120_s3, shift_add_121_s0,
       shift_add_121_s1, shift_add_121_s2, shift_add_121_s3, shift_add_122_s0, shift_add_122_s1,
       shift_add_122_s2, shift_add_122_s3, shift_add_123_s0, shift_add_123_s1, shift_add_123_s2,
       shift_add_123_s3, shift_add_124_s0, shift_add_124_s1, shift_add_124_s2, shift_add_124_s3,
       shift_add_125_s0, shift_add_125_s1, shift_add_125_s2, shift_add_125_s3, shift_add_126_s0,
       shift_add_126_s1, shift_add_126_s2, shift_add_126_s3, shift_add_127_s0, shift_add_127_s1,
       shift_add_127_s2, shift_add_127_s3, shift_add_128_s0, shift_add_128_s1, shift_add_128_s2,
       shift_add_128_s3, shift_add_129_s0, shift_add_129_s1, shift_add_129_s2, shift_add_129_s3,
       shift_add_130_s0, shift_add_130_s1, shift_add_130_s2, shift_add_130_s3, shift_add_131_s0,
       shift_add_131_s1, shift_add_131_s2, shift_add_131_s3, shift_add_132_s0, shift_add_132_s1,
       shift_add_132_s2, shift_add_132_s3, shift_add_133_s0, shift_add_133_s1, shift_add_133_s2,
       shift_add_133_s3, shift_add_134_s0, shift_add_134_s1, shift_add_134_s2, shift_add_134_s3,
       shift_add_135_s0, shift_add_135_s1, shift_add_135_s2, shift_add_135_s3, shift_add_137_s0,
       shift_add_137_s1, shift_add_137_s2, shift_add_137_s3, shift_add_139_s0, shift_add_139_s1,
       shift_add_139_s2, shift_add_139_s3, shift_add_141_s0, shift_add_141_s1, shift_add_141_s2,
       shift_add_141_s3, shift_add_143_s0, shift_add_143_s1, shift_add_143_s2, shift_add_143_s3,
       shift_add_145_s0, shift_add_145_s1, shift_add_145_s2, shift_add_145_s3, shift_add_147_s0,
       shift_add_147_s1, shift_add_147_s2, shift_add_147_s3, shift_add_149_s0, shift_add_149_s1,
       shift_add_149_s2, shift_add_149_s3, shift_add_151_s0, shift_add_151_s1, shift_add_151_s2,
       shift_add_151_s3, shift_add_153_s0, shift_add_153_s1, shift_add_153_s2, shift_add_153_s3,
       shift_add_155_s0, shift_add_155_s1, shift_add_155_s2;

  SHIFT_ADD shift_add_1 (
    .A2(A[31]), .A3(1'b0), .A0(A[29]), .A1(A[30]), .S2(shift_add_1_s2), .S3(shift_add_1_s3),
    .S0(shift_add_1_s0), .S1(shift_add_1_s1));
  SHIFT_ADD shift_add_2 (
    .A2(shift_add_1_s1), .A3(shift_add_1_s2), .A0(A[28]), .A1(shift_add_1_s0), .S2(shift_add_2_s2),
    .S3(shift_add_2_s3), .S0(shift_add_2_s0), .S1(shift_add_2_s1));
  SHIFT_ADD shift_add_3 (
    .A2(shift_add_2_s1), .A3(shift_add_2_s2), .A0(A[27]), .A1(shift_add_2_s0), .S2(shift_add_3_s2),
    .S3(shift_add_3_s3), .S0(shift_add_3_s0), .S1(shift_add_3_s1));
  SHIFT_ADD shift_add_4 (
    .A2(shift_add_5_s1), .A3(shift_add_5_s2), .A0(A[25]), .A1(shift_add_5_s0), .S2(shift_add_4_s2),
    .S3(shift_add_4_s3), .S0(shift_add_4_s0), .S1(shift_add_4_s1));
  SHIFT_ADD shift_add_5 (
    .A2(shift_add_3_s1), .A3(shift_add_3_s2), .A0(A[26]), .A1(shift_add_3_s0), .S2(shift_add_5_s2),
    .S3(shift_add_5_s3), .S0(shift_add_5_s0), .S1(shift_add_5_s1));
  SHIFT_ADD shift_add_6 (
    .A2(shift_add_7_s1), .A3(shift_add_7_s2), .A0(shift_add_5_s3), .A1(shift_add_7_s0), .S2(shift_add_6_s2),
    .S3(shift_add_6_s3), .S0(shift_add_6_s0), .S1(shift_add_6_s1));
  SHIFT_ADD shift_add_7 (
    .A2(shift_add_1_s3), .A3(1'b0), .A0(shift_add_3_s3), .A1(shift_add_2_s3), .S2(shift_add_7_s2),
    .S3(shift_add_7_s3), .S0(shift_add_7_s0), .S1(shift_add_7_s1));
  SHIFT_ADD shift_add_8 (
    .A2(shift_add_4_s1), .A3(shift_add_4_s2), .A0(A[24]), .A1(shift_add_4_s0), .S2(shift_add_8_s2),
    .S3(shift_add_8_s3), .S0(shift_add_8_s0), .S1(shift_add_8_s1));
  SHIFT_ADD shift_add_9 (
    .A2(shift_add_6_s1), .A3(shift_add_6_s2), .A0(shift_add_4_s3), .A1(shift_add_6_s0), .S2(shift_add_9_s2),
    .S3(shift_add_9_s3), .S0(shift_add_9_s0), .S1(shift_add_9_s1));
  SHIFT_ADD shift_add_10 (
    .A2(shift_add_8_s1), .A3(shift_add_8_s2), .A0(A[23]), .A1(shift_add_8_s0), .S2(shift_add_10_s2),
    .S3(shift_add_10_s3), .S0(shift_add_10_s0), .S1(shift_add_10_s1));
  SHIFT_ADD shift_add_11 (
    .A2(shift_add_9_s1), .A3(shift_add_9_s2), .A0(shift_add_8_s3), .A1(shift_add_9_s0), .S2(shift_add_11_s2),
    .S3(shift_add_11_s3), .S0(shift_add_11_s0), .S1(shift_add_11_s1));
  SHIFT_ADD shift_add_12 (
    .A2(shift_add_7_s3), .A3(1'b0), .A0(shift_add_9_s3), .A1(shift_add_6_s3), .S2(shift_add_12_s2),
    .S3(shift_add_12_s3), .S0(shift_add_12_s0), .S1(shift_add_12_s1));
  SHIFT_ADD shift_add_13 (
    .A2(shift_add_14_s1), .A3(shift_add_14_s2), .A0(A[21]), .A1(shift_add_14_s0), .S2(shift_add_13_s2),
    .S3(shift_add_13_s3), .S0(shift_add_13_s0), .S1(shift_add_13_s1));
  SHIFT_ADD shift_add_14 (
    .A2(shift_add_10_s1), .A3(shift_add_10_s2), .A0(A[22]), .A1(shift_add_10_s0), .S2(shift_add_14_s2),
    .S3(shift_add_14_s3), .S0(shift_add_14_s0), .S1(shift_add_14_s1));
  SHIFT_ADD shift_add_15 (
    .A2(shift_add_16_s1), .A3(shift_add_16_s2), .A0(shift_add_14_s3), .A1(shift_add_16_s0),
    .S2(shift_add_15_s2), .S3(shift_add_15_s3), .S0(shift_add_15_s0), .S1(shift_add_15_s1));
  SHIFT_ADD shift_add_16 (
    .A2(shift_add_11_s1), .A3(shift_add_11_s2), .A0(shift_add_10_s3), .A1(shift_add_11_s0),
    .S2(shift_add_16_s2), .S3(shift_add_16_s3), .S0(shift_add_16_s0), .S1(shift_add_16_s1));
  SHIFT_ADD shift_add_17 (
    .A2(shift_add_18_s1), .A3(shift_add_18_s2), .A0(shift_add_16_s3), .A1(shift_add_18_s0),
    .S2(shift_add_17_s2), .S3(shift_add_17_s3), .S0(shift_add_17_s0), .S1(shift_add_17_s1));
  SHIFT_ADD shift_add_18 (
    .A2(shift_add_12_s1), .A3(shift_add_12_s2), .A0(shift_add_11_s3), .A1(shift_add_12_s0),
    .S2(shift_add_18_s2), .S3(shift_add_18_s3), .S0(shift_add_18_s0), .S1(shift_add_18_s1));
  SHIFT_ADD shift_add_19 (
    .A2(shift_add_13_s1), .A3(shift_add_13_s2), .A0(A[20]), .A1(shift_add_13_s0), .S2(shift_add_19_s2),
    .S3(shift_add_19_s3), .S0(shift_add_19_s0), .S1(shift_add_19_s1));
  SHIFT_ADD shift_add_20 (
    .A2(shift_add_15_s1), .A3(shift_add_15_s2), .A0(shift_add_13_s3), .A1(shift_add_15_s0),
    .S2(shift_add_20_s2), .S3(shift_add_20_s3), .S0(shift_add_20_s0), .S1(shift_add_20_s1));
  SHIFT_ADD shift_add_21 (
    .A2(shift_add_17_s1), .A3(shift_add_17_s2), .A0(shift_add_15_s3), .A1(shift_add_17_s0),
    .S2(shift_add_21_s2), .S3(shift_add_21_s3), .S0(shift_add_21_s0), .S1(shift_add_21_s1));
  SHIFT_ADD shift_add_22 (
    .A2(shift_add_12_s3), .A3(1'b0), .A0(shift_add_17_s3), .A1(shift_add_18_s3), .S2(shift_add_22_s2),
    .S3(shift_add_22_s3), .S0(shift_add_22_s0), .S1(shift_add_22_s1));
  SHIFT_ADD shift_add_23 (
    .A2(shift_add_19_s1), .A3(shift_add_19_s2), .A0(A[19]), .A1(shift_add_19_s0), .S2(shift_add_23_s2),
    .S3(shift_add_23_s3), .S0(shift_add_23_s0), .S1(shift_add_23_s1));
  SHIFT_ADD shift_add_24 (
    .A2(shift_add_20_s1), .A3(shift_add_20_s2), .A0(shift_add_19_s3), .A1(shift_add_20_s0),
    .S2(shift_add_24_s2), .S3(shift_add_24_s3), .S0(shift_add_24_s0), .S1(shift_add_24_s1));
  SHIFT_ADD shift_add_25 (
    .A2(shift_add_21_s1), .A3(shift_add_21_s2), .A0(shift_add_20_s3), .A1(shift_add_21_s0),
    .S2(shift_add_25_s2), .S3(shift_add_25_s3), .S0(shift_add_25_s0), .S1(shift_add_25_s1));
  SHIFT_ADD shift_add_26 (
    .A2(shift_add_22_s1), .A3(shift_add_22_s2), .A0(shift_add_21_s3), .A1(shift_add_22_s0),
    .S2(shift_add_26_s2), .S3(shift_add_26_s3), .S0(shift_add_26_s0), .S1(shift_add_26_s1));
  SHIFT_ADD shift_add_27 (
    .A2(shift_add_28_s1), .A3(shift_add_28_s2), .A0(A[17]), .A1(shift_add_28_s0), .S2(shift_add_27_s2),
    .S3(shift_add_27_s3), .S0(shift_add_27_s0), .S1(shift_add_27_s1));
  SHIFT_ADD shift_add_28 (
    .A2(shift_add_23_s1), .A3(shift_add_23_s2), .A0(A[18]), .A1(shift_add_23_s0), .S2(shift_add_28_s2),
    .S3(shift_add_28_s3), .S0(shift_add_28_s0), .S1(shift_add_28_s1));
  SHIFT_ADD shift_add_29 (
    .A2(shift_add_30_s1), .A3(shift_add_30_s2), .A0(shift_add_28_s3), .A1(shift_add_30_s0),
    .S2(shift_add_29_s2), .S3(shift_add_29_s3), .S0(shift_add_29_s0), .S1(shift_add_29_s1));
  SHIFT_ADD shift_add_30 (
    .A2(shift_add_24_s1), .A3(shift_add_24_s2), .A0(shift_add_23_s3), .A1(shift_add_24_s0),
    .S2(shift_add_30_s2), .S3(shift_add_30_s3), .S0(shift_add_30_s0), .S1(shift_add_30_s1));
  SHIFT_ADD shift_add_31 (
    .A2(shift_add_32_s1), .A3(shift_add_32_s2), .A0(shift_add_30_s3), .A1(shift_add_32_s0),
    .S2(shift_add_31_s2), .S3(shift_add_31_s3), .S0(shift_add_31_s0), .S1(shift_add_31_s1));
  SHIFT_ADD shift_add_32 (
    .A2(shift_add_25_s1), .A3(shift_add_25_s2), .A0(shift_add_24_s3), .A1(shift_add_25_s0),
    .S2(shift_add_32_s2), .S3(shift_add_32_s3), .S0(shift_add_32_s0), .S1(shift_add_32_s1));
  SHIFT_ADD shift_add_33 (
    .A2(shift_add_34_s1), .A3(shift_add_34_s2), .A0(shift_add_32_s3), .A1(shift_add_34_s0),
    .S2(shift_add_33_s2), .S3(shift_add_33_s3), .S0(shift_add_33_s0), .S1(shift_add_33_s1));
  SHIFT_ADD shift_add_34 (
    .A2(shift_add_26_s1), .A3(shift_add_26_s2), .A0(shift_add_25_s3), .A1(shift_add_26_s0),
    .S2(shift_add_34_s2), .S3(shift_add_34_s3), .S0(shift_add_34_s0), .S1(shift_add_34_s1));
  SHIFT_ADD shift_add_35 (
    .A2(shift_add_22_s3), .A3(1'b0), .A0(shift_add_34_s3), .A1(shift_add_26_s3), .S2(shift_add_35_s2),
    .S3(shift_add_35_s3), .S0(shift_add_35_s0), .S1(shift_add_35_s1));
  SHIFT_ADD shift_add_36 (
    .A2(shift_add_27_s1), .A3(shift_add_27_s2), .A0(A[16]), .A1(shift_add_27_s0), .S2(shift_add_36_s2),
    .S3(shift_add_36_s3), .S0(shift_add_36_s0), .S1(shift_add_36_s1));
  SHIFT_ADD shift_add_37 (
    .A2(shift_add_29_s1), .A3(shift_add_29_s2), .A0(shift_add_27_s3), .A1(shift_add_29_s0),
    .S2(shift_add_37_s2), .S3(shift_add_37_s3), .S0(shift_add_37_s0), .S1(shift_add_37_s1));
  SHIFT_ADD shift_add_38 (
    .A2(shift_add_31_s1), .A3(shift_add_31_s2), .A0(shift_add_29_s3), .A1(shift_add_31_s0),
    .S2(shift_add_38_s2), .S3(shift_add_38_s3), .S0(shift_add_38_s0), .S1(shift_add_38_s1));
  SHIFT_ADD shift_add_39 (
    .A2(shift_add_33_s1), .A3(shift_add_33_s2), .A0(shift_add_31_s3), .A1(shift_add_33_s0),
    .S2(shift_add_39_s2), .S3(shift_add_39_s3), .S0(shift_add_39_s0), .S1(shift_add_39_s1));
  SHIFT_ADD shift_add_40 (
    .A2(shift_add_35_s1), .A3(shift_add_35_s2), .A0(shift_add_33_s3), .A1(shift_add_35_s0),
    .S2(shift_add_40_s2), .S3(shift_add_40_s3), .S0(shift_add_40_s0), .S1(shift_add_40_s1));
  SHIFT_ADD shift_add_41 (
    .A2(shift_add_36_s1), .A3(shift_add_36_s2), .A0(A[15]), .A1(shift_add_36_s0), .S2(shift_add_41_s2),
    .S3(shift_add_41_s3), .S0(shift_add_41_s0), .S1(shift_add_41_s1));
  SHIFT_ADD shift_add_42 (
    .A2(shift_add_37_s1), .A3(shift_add_37_s2), .A0(shift_add_36_s3), .A1(shift_add_37_s0),
    .S2(shift_add_42_s2), .S3(shift_add_42_s3), .S0(shift_add_42_s0), .S1(shift_add_42_s1));
  SHIFT_ADD shift_add_43 (
    .A2(shift_add_38_s1), .A3(shift_add_38_s2), .A0(shift_add_37_s3), .A1(shift_add_38_s0),
    .S2(shift_add_43_s2), .S3(shift_add_43_s3), .S0(shift_add_43_s0), .S1(shift_add_43_s1));
  SHIFT_ADD shift_add_44 (
    .A2(shift_add_39_s1), .A3(shift_add_39_s2), .A0(shift_add_38_s3), .A1(shift_add_39_s0),
    .S2(shift_add_44_s2), .S3(shift_add_44_s3), .S0(shift_add_44_s0), .S1(shift_add_44_s1));
  SHIFT_ADD shift_add_45 (
    .A2(shift_add_40_s1), .A3(shift_add_40_s2), .A0(shift_add_39_s3), .A1(shift_add_40_s0),
    .S2(shift_add_45_s2), .S3(shift_add_45_s3), .S0(shift_add_45_s0), .S1(shift_add_45_s1));
  SHIFT_ADD shift_add_46 (
    .A2(shift_add_47_s1), .A3(shift_add_47_s2), .A0(A[13]), .A1(shift_add_47_s0), .S2(shift_add_46_s2),
    .S3(shift_add_46_s3), .S0(shift_add_46_s0), .S1(shift_add_46_s1));
  SHIFT_ADD shift_add_47 (
    .A2(shift_add_41_s1), .A3(shift_add_41_s2), .A0(A[14]), .A1(shift_add_41_s0), .S2(shift_add_47_s2),
    .S3(shift_add_47_s3), .S0(shift_add_47_s0), .S1(shift_add_47_s1));
  SHIFT_ADD shift_add_48 (
    .A2(shift_add_49_s1), .A3(shift_add_49_s2), .A0(shift_add_47_s3), .A1(shift_add_49_s0),
    .S2(shift_add_48_s2), .S3(shift_add_48_s3), .S0(shift_add_48_s0), .S1(shift_add_48_s1));
  SHIFT_ADD shift_add_49 (
    .A2(shift_add_42_s1), .A3(shift_add_42_s2), .A0(shift_add_41_s3), .A1(shift_add_42_s0),
    .S2(shift_add_49_s2), .S3(shift_add_49_s3), .S0(shift_add_49_s0), .S1(shift_add_49_s1));
  SHIFT_ADD shift_add_50 (
    .A2(shift_add_51_s1), .A3(shift_add_51_s2), .A0(shift_add_49_s3), .A1(shift_add_51_s0),
    .S2(shift_add_50_s2), .S3(shift_add_50_s3), .S0(shift_add_50_s0), .S1(shift_add_50_s1));
  SHIFT_ADD shift_add_51 (
    .A2(shift_add_43_s1), .A3(shift_add_43_s2), .A0(shift_add_42_s3), .A1(shift_add_43_s0),
    .S2(shift_add_51_s2), .S3(shift_add_51_s3), .S0(shift_add_51_s0), .S1(shift_add_51_s1));
  SHIFT_ADD shift_add_52 (
    .A2(shift_add_53_s1), .A3(shift_add_53_s2), .A0(shift_add_51_s3), .A1(shift_add_53_s0),
    .S2(shift_add_52_s2), .S3(shift_add_52_s3), .S0(shift_add_52_s0), .S1(shift_add_52_s1));
  SHIFT_ADD shift_add_53 (
    .A2(shift_add_44_s1), .A3(shift_add_44_s2), .A0(shift_add_43_s3), .A1(shift_add_44_s0),
    .S2(shift_add_53_s2), .S3(shift_add_53_s3), .S0(shift_add_53_s0), .S1(shift_add_53_s1));
  SHIFT_ADD shift_add_54 (
    .A2(shift_add_55_s1), .A3(shift_add_55_s2), .A0(shift_add_53_s3), .A1(shift_add_55_s0),
    .S2(shift_add_54_s2), .S3(shift_add_54_s3), .S0(shift_add_54_s0), .S1(shift_add_54_s1));
  SHIFT_ADD shift_add_55 (
    .A2(shift_add_45_s1), .A3(shift_add_45_s2), .A0(shift_add_44_s3), .A1(shift_add_45_s0),
    .S2(shift_add_55_s2), .S3(shift_add_55_s3), .S0(shift_add_55_s0), .S1(shift_add_55_s1));
  SHIFT_ADD shift_add_56 (
    .A2(shift_add_57_s1), .A3(shift_add_57_s2), .A0(shift_add_55_s3), .A1(shift_add_57_s0),
    .S2(shift_add_56_s2), .S3(shift_add_56_s3), .S0(shift_add_56_s0), .S1(shift_add_56_s1));
  SHIFT_ADD shift_add_57 (
    .A2(shift_add_35_s3), .A3(1'b0), .A0(shift_add_45_s3), .A1(shift_add_40_s3), .S2(shift_add_57_s2),
    .S3(shift_add_57_s3), .S0(shift_add_57_s0), .S1(shift_add_57_s1));
  SHIFT_ADD shift_add_58 (
    .A2(shift_add_46_s1), .A3(shift_add_46_s2), .A0(A[12]), .A1(shift_add_46_s0), .S2(shift_add_58_s2),
    .S3(shift_add_58_s3), .S0(shift_add_58_s0), .S1(shift_add_58_s1));
  SHIFT_ADD shift_add_59 (
    .A2(shift_add_48_s1), .A3(shift_add_48_s2), .A0(shift_add_46_s3), .A1(shift_add_48_s0),
    .S2(shift_add_59_s2), .S3(shift_add_59_s3), .S0(shift_add_59_s0), .S1(shift_add_59_s1));
  SHIFT_ADD shift_add_60 (
    .A2(shift_add_50_s1), .A3(shift_add_50_s2), .A0(shift_add_48_s3), .A1(shift_add_50_s0),
    .S2(shift_add_60_s2), .S3(shift_add_60_s3), .S0(shift_add_60_s0), .S1(shift_add_60_s1));
  SHIFT_ADD shift_add_61 (
    .A2(shift_add_52_s1), .A3(shift_add_52_s2), .A0(shift_add_50_s3), .A1(shift_add_52_s0),
    .S2(shift_add_61_s2), .S3(shift_add_61_s3), .S0(shift_add_61_s0), .S1(shift_add_61_s1));
  SHIFT_ADD shift_add_62 (
    .A2(shift_add_54_s1), .A3(shift_add_54_s2), .A0(shift_add_52_s3), .A1(shift_add_54_s0),
    .S2(shift_add_62_s2), .S3(shift_add_62_s3), .S0(shift_add_62_s0), .S1(shift_add_62_s1));
  SHIFT_ADD shift_add_63 (
    .A2(shift_add_56_s1), .A3(shift_add_56_s2), .A0(shift_add_54_s3), .A1(shift_add_56_s0),
    .S2(shift_add_63_s2), .S3(shift_add_63_s3), .S0(shift_add_63_s0), .S1(shift_add_63_s1));
  SHIFT_ADD shift_add_64 (
    .A2(shift_add_58_s1), .A3(shift_add_58_s2), .A0(A[11]), .A1(shift_add_58_s0), .S2(shift_add_64_s2),
    .S3(shift_add_64_s3), .S0(shift_add_64_s0), .S1(shift_add_64_s1));
  SHIFT_ADD shift_add_65 (
    .A2(shift_add_59_s1), .A3(shift_add_59_s2), .A0(shift_add_58_s3), .A1(shift_add_59_s0),
    .S2(shift_add_65_s2), .S3(shift_add_65_s3), .S0(shift_add_65_s0), .S1(shift_add_65_s1));
  SHIFT_ADD shift_add_66 (
    .A2(shift_add_60_s1), .A3(shift_add_60_s2), .A0(shift_add_59_s3), .A1(shift_add_60_s0),
    .S2(shift_add_66_s2), .S3(shift_add_66_s3), .S0(shift_add_66_s0), .S1(shift_add_66_s1));
  SHIFT_ADD shift_add_67 (
    .A2(shift_add_61_s1), .A3(shift_add_61_s2), .A0(shift_add_60_s3), .A1(shift_add_61_s0),
    .S2(shift_add_67_s2), .S3(shift_add_67_s3), .S0(shift_add_67_s0), .S1(shift_add_67_s1));
  SHIFT_ADD shift_add_68 (
    .A2(shift_add_62_s1), .A3(shift_add_62_s2), .A0(shift_add_61_s3), .A1(shift_add_62_s0),
    .S2(shift_add_68_s2), .S3(shift_add_68_s3), .S0(shift_add_68_s0), .S1(shift_add_68_s1));
  SHIFT_ADD shift_add_69 (
    .A2(shift_add_63_s1), .A3(shift_add_63_s2), .A0(shift_add_62_s3), .A1(shift_add_63_s0),
    .S2(shift_add_69_s2), .S3(shift_add_69_s3), .S0(shift_add_69_s0), .S1(shift_add_69_s1));
  SHIFT_ADD shift_add_70 (
    .A2(shift_add_57_s3), .A3(1'b0), .A0(shift_add_63_s3), .A1(shift_add_56_s3), .S2(shift_add_70_s2),
    .S3(shift_add_70_s3), .S0(shift_add_70_s0), .S1(shift_add_70_s1));
  SHIFT_ADD shift_add_71 (
    .A2(shift_add_72_s1), .A3(shift_add_72_s2), .A0(A[9]), .A1(shift_add_72_s0), .S2(shift_add_71_s2),
    .S3(shift_add_71_s3), .S0(shift_add_71_s0), .S1(shift_add_71_s1));
  SHIFT_ADD shift_add_72 (
    .A2(shift_add_64_s1), .A3(shift_add_64_s2), .A0(A[10]), .A1(shift_add_64_s0), .S2(shift_add_72_s2),
    .S3(shift_add_72_s3), .S0(shift_add_72_s0), .S1(shift_add_72_s1));
  SHIFT_ADD shift_add_73 (
    .A2(shift_add_74_s1), .A3(shift_add_74_s2), .A0(shift_add_72_s3), .A1(shift_add_74_s0),
    .S2(shift_add_73_s2), .S3(shift_add_73_s3), .S0(shift_add_73_s0), .S1(shift_add_73_s1));
  SHIFT_ADD shift_add_74 (
    .A2(shift_add_65_s1), .A3(shift_add_65_s2), .A0(shift_add_64_s3), .A1(shift_add_65_s0),
    .S2(shift_add_74_s2), .S3(shift_add_74_s3), .S0(shift_add_74_s0), .S1(shift_add_74_s1));
  SHIFT_ADD shift_add_75 (
    .A2(shift_add_76_s1), .A3(shift_add_76_s2), .A0(shift_add_74_s3), .A1(shift_add_76_s0),
    .S2(shift_add_75_s2), .S3(shift_add_75_s3), .S0(shift_add_75_s0), .S1(shift_add_75_s1));
  SHIFT_ADD shift_add_76 (
    .A2(shift_add_66_s1), .A3(shift_add_66_s2), .A0(shift_add_65_s3), .A1(shift_add_66_s0),
    .S2(shift_add_76_s2), .S3(shift_add_76_s3), .S0(shift_add_76_s0), .S1(shift_add_76_s1));
  SHIFT_ADD shift_add_77 (
    .A2(shift_add_78_s1), .A3(shift_add_78_s2), .A0(shift_add_76_s3), .A1(shift_add_78_s0),
    .S2(shift_add_77_s2), .S3(shift_add_77_s3), .S0(shift_add_77_s0), .S1(shift_add_77_s1));
  SHIFT_ADD shift_add_78 (
    .A2(shift_add_67_s1), .A3(shift_add_67_s2), .A0(shift_add_66_s3), .A1(shift_add_67_s0),
    .S2(shift_add_78_s2), .S3(shift_add_78_s3), .S0(shift_add_78_s0), .S1(shift_add_78_s1));
  SHIFT_ADD shift_add_79 (
    .A2(shift_add_80_s1), .A3(shift_add_80_s2), .A0(shift_add_78_s3), .A1(shift_add_80_s0),
    .S2(shift_add_79_s2), .S3(shift_add_79_s3), .S0(shift_add_79_s0), .S1(shift_add_79_s1));
  SHIFT_ADD shift_add_80 (
    .A2(shift_add_68_s1), .A3(shift_add_68_s2), .A0(shift_add_67_s3), .A1(shift_add_68_s0),
    .S2(shift_add_80_s2), .S3(shift_add_80_s3), .S0(shift_add_80_s0), .S1(shift_add_80_s1));
  SHIFT_ADD shift_add_81 (
    .A2(shift_add_82_s1), .A3(shift_add_82_s2), .A0(shift_add_80_s3), .A1(shift_add_82_s0),
    .S2(shift_add_81_s2), .S3(shift_add_81_s3), .S0(shift_add_81_s0), .S1(shift_add_81_s1));
  SHIFT_ADD shift_add_82 (
    .A2(shift_add_69_s1), .A3(shift_add_69_s2), .A0(shift_add_68_s3), .A1(shift_add_69_s0),
    .S2(shift_add_82_s2), .S3(shift_add_82_s3), .S0(shift_add_82_s0), .S1(shift_add_82_s1));
  SHIFT_ADD shift_add_83 (
    .A2(shift_add_84_s1), .A3(shift_add_84_s2), .A0(shift_add_82_s3), .A1(shift_add_84_s0),
    .S2(shift_add_83_s2), .S3(shift_add_83_s3), .S0(shift_add_83_s0), .S1(shift_add_83_s1));
  SHIFT_ADD shift_add_84 (
    .A2(shift_add_70_s1), .A3(shift_add_70_s2), .A0(shift_add_69_s3), .A1(shift_add_70_s0),
    .S2(shift_add_84_s2), .S3(shift_add_84_s3), .S0(shift_add_84_s0), .S1(shift_add_84_s1));
  SHIFT_ADD shift_add_85 (
    .A2(shift_add_71_s1), .A3(shift_add_71_s2), .A0(A[8]), .A1(shift_add_71_s0), .S2(shift_add_85_s2),
    .S3(shift_add_85_s3), .S0(shift_add_85_s0), .S1(shift_add_85_s1));
  SHIFT_ADD shift_add_86 (
    .A2(shift_add_73_s1), .A3(shift_add_73_s2), .A0(shift_add_71_s3), .A1(shift_add_73_s0),
    .S2(shift_add_86_s2), .S3(shift_add_86_s3), .S0(shift_add_86_s0), .S1(shift_add_86_s1));
  SHIFT_ADD shift_add_87 (
    .A2(shift_add_75_s1), .A3(shift_add_75_s2), .A0(shift_add_73_s3), .A1(shift_add_75_s0),
    .S2(shift_add_87_s2), .S3(shift_add_87_s3), .S0(shift_add_87_s0), .S1(shift_add_87_s1));
  SHIFT_ADD shift_add_88 (
    .A2(shift_add_77_s1), .A3(shift_add_77_s2), .A0(shift_add_75_s3), .A1(shift_add_77_s0),
    .S2(shift_add_88_s2), .S3(shift_add_88_s3), .S0(shift_add_88_s0), .S1(shift_add_88_s1));
  SHIFT_ADD shift_add_89 (
    .A2(shift_add_79_s1), .A3(shift_add_79_s2), .A0(shift_add_77_s3), .A1(shift_add_79_s0),
    .S2(shift_add_89_s2), .S3(shift_add_89_s3), .S0(shift_add_89_s0), .S1(shift_add_89_s1));
  SHIFT_ADD shift_add_90 (
    .A2(shift_add_81_s1), .A3(shift_add_81_s2), .A0(shift_add_79_s3), .A1(shift_add_81_s0),
    .S2(shift_add_90_s2), .S3(shift_add_90_s3), .S0(shift_add_90_s0), .S1(shift_add_90_s1));
  SHIFT_ADD shift_add_91 (
    .A2(shift_add_83_s1), .A3(shift_add_83_s2), .A0(shift_add_81_s3), .A1(shift_add_83_s0),
    .S2(shift_add_91_s2), .S3(shift_add_91_s3), .S0(shift_add_91_s0), .S1(shift_add_91_s1));
  SHIFT_ADD shift_add_92 (
    .A2(shift_add_70_s3), .A3(1'b0), .A0(shift_add_83_s3), .A1(shift_add_84_s3), .S2(shift_add_92_s2),
    .S3(shift_add_92_s3), .S0(shift_add_92_s0), .S1(shift_add_92_s1));
  SHIFT_ADD shift_add_93 (
    .A2(shift_add_85_s1), .A3(shift_add_85_s2), .A0(A[7]), .A1(shift_add_85_s0), .S2(shift_add_93_s2),
    .S3(shift_add_93_s3), .S0(shift_add_93_s0), .S1(shift_add_93_s1));
  SHIFT_ADD shift_add_94 (
    .A2(shift_add_86_s1), .A3(shift_add_86_s2), .A0(shift_add_85_s3), .A1(shift_add_86_s0),
    .S2(shift_add_94_s2), .S3(shift_add_94_s3), .S0(shift_add_94_s0), .S1(shift_add_94_s1));
  SHIFT_ADD shift_add_95 (
    .A2(shift_add_87_s1), .A3(shift_add_87_s2), .A0(shift_add_86_s3), .A1(shift_add_87_s0),
    .S2(shift_add_95_s2), .S3(shift_add_95_s3), .S0(shift_add_95_s0), .S1(shift_add_95_s1));
  SHIFT_ADD shift_add_96 (
    .A2(shift_add_88_s1), .A3(shift_add_88_s2), .A0(shift_add_87_s3), .A1(shift_add_88_s0),
    .S2(shift_add_96_s2), .S3(shift_add_96_s3), .S0(shift_add_96_s0), .S1(shift_add_96_s1));
  SHIFT_ADD shift_add_97 (
    .A2(shift_add_89_s1), .A3(shift_add_89_s2), .A0(shift_add_88_s3), .A1(shift_add_89_s0),
    .S2(shift_add_97_s2), .S3(shift_add_97_s3), .S0(shift_add_97_s0), .S1(shift_add_97_s1));
  SHIFT_ADD shift_add_98 (
    .A2(shift_add_90_s1), .A3(shift_add_90_s2), .A0(shift_add_89_s3), .A1(shift_add_90_s0),
    .S2(shift_add_98_s2), .S3(shift_add_98_s3), .S0(shift_add_98_s0), .S1(shift_add_98_s1));
  SHIFT_ADD shift_add_99 (
    .A2(shift_add_91_s1), .A3(shift_add_91_s2), .A0(shift_add_90_s3), .A1(shift_add_91_s0),
    .S2(shift_add_99_s2), .S3(shift_add_99_s3), .S0(shift_add_99_s0), .S1(shift_add_99_s1));
  SHIFT_ADD shift_add_100 (
    .A2(shift_add_92_s1), .A3(shift_add_92_s2), .A0(shift_add_91_s3), .A1(shift_add_92_s0),
    .S2(shift_add_100_s2), .S3(shift_add_100_s3), .S0(shift_add_100_s0), .S1(shift_add_100_s1));
  SHIFT_ADD shift_add_101 (
    .A2(shift_add_102_s1), .A3(shift_add_102_s2), .A0(A[5]), .A1(shift_add_102_s0), .S2(shift_add_101_s2),
    .S3(shift_add_101_s3), .S0(shift_add_101_s0), .S1(shift_add_101_s1));
  SHIFT_ADD shift_add_102 (
    .A2(shift_add_93_s1), .A3(shift_add_93_s2), .A0(A[6]), .A1(shift_add_93_s0), .S2(shift_add_102_s2),
    .S3(shift_add_102_s3), .S0(shift_add_102_s0), .S1(shift_add_102_s1));
  SHIFT_ADD shift_add_103 (
    .A2(shift_add_104_s1), .A3(shift_add_104_s2), .A0(shift_add_102_s3), .A1(shift_add_104_s0),
    .S2(shift_add_103_s2), .S3(shift_add_103_s3), .S0(shift_add_103_s0), .S1(shift_add_103_s1));
  SHIFT_ADD shift_add_104 (
    .A2(shift_add_94_s1), .A3(shift_add_94_s2), .A0(shift_add_93_s3), .A1(shift_add_94_s0),
    .S2(shift_add_104_s2), .S3(shift_add_104_s3), .S0(shift_add_104_s0), .S1(shift_add_104_s1));
  SHIFT_ADD shift_add_105 (
    .A2(shift_add_106_s1), .A3(shift_add_106_s2), .A0(shift_add_104_s3), .A1(shift_add_106_s0),
    .S2(shift_add_105_s2), .S3(shift_add_105_s3), .S0(shift_add_105_s0), .S1(shift_add_105_s1));
  SHIFT_ADD shift_add_106 (
    .A2(shift_add_95_s1), .A3(shift_add_95_s2), .A0(shift_add_94_s3), .A1(shift_add_95_s0),
    .S2(shift_add_106_s2), .S3(shift_add_106_s3), .S0(shift_add_106_s0), .S1(shift_add_106_s1));
  SHIFT_ADD shift_add_107 (
    .A2(shift_add_108_s1), .A3(shift_add_108_s2), .A0(shift_add_106_s3), .A1(shift_add_108_s0),
    .S2(shift_add_107_s2), .S3(shift_add_107_s3), .S0(shift_add_107_s0), .S1(shift_add_107_s1));
  SHIFT_ADD shift_add_108 (
    .A2(shift_add_96_s1), .A3(shift_add_96_s2), .A0(shift_add_95_s3), .A1(shift_add_96_s0),
    .S2(shift_add_108_s2), .S3(shift_add_108_s3), .S0(shift_add_108_s0), .S1(shift_add_108_s1));
  SHIFT_ADD shift_add_109 (
    .A2(shift_add_110_s1), .A3(shift_add_110_s2), .A0(shift_add_108_s3), .A1(shift_add_110_s0),
    .S2(shift_add_109_s2), .S3(shift_add_109_s3), .S0(shift_add_109_s0), .S1(shift_add_109_s1));
  SHIFT_ADD shift_add_110 (
    .A2(shift_add_97_s1), .A3(shift_add_97_s2), .A0(shift_add_96_s3), .A1(shift_add_97_s0),
    .S2(shift_add_110_s2), .S3(shift_add_110_s3), .S0(shift_add_110_s0), .S1(shift_add_110_s1));
  SHIFT_ADD shift_add_111 (
    .A2(shift_add_112_s1), .A3(shift_add_112_s2), .A0(shift_add_110_s3), .A1(shift_add_112_s0),
    .S2(shift_add_111_s2), .S3(shift_add_111_s3), .S0(shift_add_111_s0), .S1(shift_add_111_s1));
  SHIFT_ADD shift_add_112 (
    .A2(shift_add_98_s1), .A3(shift_add_98_s2), .A0(shift_add_97_s3), .A1(shift_add_98_s0),
    .S2(shift_add_112_s2), .S3(shift_add_112_s3), .S0(shift_add_112_s0), .S1(shift_add_112_s1));
  SHIFT_ADD shift_add_113 (
    .A2(shift_add_114_s1), .A3(shift_add_114_s2), .A0(shift_add_112_s3), .A1(shift_add_114_s0),
    .S2(shift_add_113_s2), .S3(shift_add_113_s3), .S0(shift_add_113_s0), .S1(shift_add_113_s1));
  SHIFT_ADD shift_add_114 (
    .A2(shift_add_99_s1), .A3(shift_add_99_s2), .A0(shift_add_98_s3), .A1(shift_add_99_s0),
    .S2(shift_add_114_s2), .S3(shift_add_114_s3), .S0(shift_add_114_s0), .S1(shift_add_114_s1));
  SHIFT_ADD shift_add_115 (
    .A2(shift_add_116_s1), .A3(shift_add_116_s2), .A0(shift_add_114_s3), .A1(shift_add_116_s0),
    .S2(shift_add_115_s2), .S3(shift_add_115_s3), .S0(shift_add_115_s0), .S1(shift_add_115_s1));
  SHIFT_ADD shift_add_116 (
    .A2(shift_add_100_s1), .A3(shift_add_100_s2), .A0(shift_add_99_s3), .A1(shift_add_100_s0),
    .S2(shift_add_116_s2), .S3(shift_add_116_s3), .S0(shift_add_116_s0), .S1(shift_add_116_s1));
  SHIFT_ADD shift_add_117 (
    .A2(shift_add_92_s3), .A3(1'b0), .A0(shift_add_116_s3), .A1(shift_add_100_s3), .S2(shift_add_117_s2),
    .S3(shift_add_117_s3), .S0(shift_add_117_s0), .S1(shift_add_117_s1));
  SHIFT_ADD shift_add_118 (
    .A2(shift_add_101_s1), .A3(shift_add_101_s2), .A0(A[4]), .A1(shift_add_101_s0), .S2(shift_add_118_s2),
    .S3(shift_add_118_s3), .S0(shift_add_118_s0), .S1(shift_add_118_s1));
  SHIFT_ADD shift_add_119 (
    .A2(shift_add_103_s1), .A3(shift_add_103_s2), .A0(shift_add_101_s3), .A1(shift_add_103_s0),
    .S2(shift_add_119_s2), .S3(shift_add_119_s3), .S0(shift_add_119_s0), .S1(shift_add_119_s1));
  SHIFT_ADD shift_add_120 (
    .A2(shift_add_105_s1), .A3(shift_add_105_s2), .A0(shift_add_103_s3), .A1(shift_add_105_s0),
    .S2(shift_add_120_s2), .S3(shift_add_120_s3), .S0(shift_add_120_s0), .S1(shift_add_120_s1));
  SHIFT_ADD shift_add_121 (
    .A2(shift_add_107_s1), .A3(shift_add_107_s2), .A0(shift_add_105_s3), .A1(shift_add_107_s0),
    .S2(shift_add_121_s2), .S3(shift_add_121_s3), .S0(shift_add_121_s0), .S1(shift_add_121_s1));
  SHIFT_ADD shift_add_122 (
    .A2(shift_add_109_s1), .A3(shift_add_109_s2), .A0(shift_add_107_s3), .A1(shift_add_109_s0),
    .S2(shift_add_122_s2), .S3(shift_add_122_s3), .S0(shift_add_122_s0), .S1(shift_add_122_s1));
  SHIFT_ADD shift_add_123 (
    .A2(shift_add_111_s1), .A3(shift_add_111_s2), .A0(shift_add_109_s3), .A1(shift_add_111_s0),
    .S2(shift_add_123_s2), .S3(shift_add_123_s3), .S0(shift_add_123_s0), .S1(shift_add_123_s1));
  SHIFT_ADD shift_add_124 (
    .A2(shift_add_113_s1), .A3(shift_add_113_s2), .A0(shift_add_111_s3), .A1(shift_add_113_s0),
    .S2(shift_add_124_s2), .S3(shift_add_124_s3), .S0(shift_add_124_s0), .S1(shift_add_124_s1));
  SHIFT_ADD shift_add_125 (
    .A2(shift_add_115_s1), .A3(shift_add_115_s2), .A0(shift_add_113_s3), .A1(shift_add_115_s0),
    .S2(shift_add_125_s2), .S3(shift_add_125_s3), .S0(shift_add_125_s0), .S1(shift_add_125_s1));
  SHIFT_ADD shift_add_126 (
    .A2(shift_add_117_s1), .A3(shift_add_117_s2), .A0(shift_add_115_s3), .A1(shift_add_117_s0),
    .S2(shift_add_126_s2), .S3(shift_add_126_s3), .S0(shift_add_126_s0), .S1(shift_add_126_s1));
  SHIFT_ADD shift_add_127 (
    .A2(shift_add_118_s1), .A3(shift_add_118_s2), .A0(A[3]), .A1(shift_add_118_s0), .S2(shift_add_127_s2),
    .S3(shift_add_127_s3), .S0(shift_add_127_s0), .S1(shift_add_127_s1));
  SHIFT_ADD shift_add_128 (
    .A2(shift_add_119_s1), .A3(shift_add_119_s2), .A0(shift_add_118_s3), .A1(shift_add_119_s0),
    .S2(shift_add_128_s2), .S3(shift_add_128_s3), .S0(shift_add_128_s0), .S1(shift_add_128_s1));
  SHIFT_ADD shift_add_129 (
    .A2(shift_add_120_s1), .A3(shift_add_120_s2), .A0(shift_add_119_s3), .A1(shift_add_120_s0),
    .S2(shift_add_129_s2), .S3(shift_add_129_s3), .S0(shift_add_129_s0), .S1(shift_add_129_s1));
  SHIFT_ADD shift_add_130 (
    .A2(shift_add_121_s1), .A3(shift_add_121_s2), .A0(shift_add_120_s3), .A1(shift_add_121_s0),
    .S2(shift_add_130_s2), .S3(shift_add_130_s3), .S0(shift_add_130_s0), .S1(shift_add_130_s1));
  SHIFT_ADD shift_add_131 (
    .A2(shift_add_122_s1), .A3(shift_add_122_s2), .A0(shift_add_121_s3), .A1(shift_add_122_s0),
    .S2(shift_add_131_s2), .S3(shift_add_131_s3), .S0(shift_add_131_s0), .S1(shift_add_131_s1));
  SHIFT_ADD shift_add_132 (
    .A2(shift_add_123_s1), .A3(shift_add_123_s2), .A0(shift_add_122_s3), .A1(shift_add_123_s0),
    .S2(shift_add_132_s2), .S3(shift_add_132_s3), .S0(shift_add_132_s0), .S1(shift_add_132_s1));
  SHIFT_ADD shift_add_133 (
    .A2(shift_add_124_s1), .A3(shift_add_124_s2), .A0(shift_add_123_s3), .A1(shift_add_124_s0),
    .S2(shift_add_133_s2), .S3(shift_add_133_s3), .S0(shift_add_133_s0), .S1(shift_add_133_s1));
  SHIFT_ADD shift_add_134 (
    .A2(shift_add_125_s1), .A3(shift_add_125_s2), .A0(shift_add_124_s3), .A1(shift_add_125_s0),
    .S2(shift_add_134_s2), .S3(shift_add_134_s3), .S0(shift_add_134_s0), .S1(shift_add_134_s1));
  SHIFT_ADD shift_add_135 (
    .A2(shift_add_126_s1), .A3(shift_add_126_s2), .A0(shift_add_125_s3), .A1(shift_add_126_s0),
    .S2(shift_add_135_s2), .S3(shift_add_135_s3), .S0(shift_add_135_s0), .S1(shift_add_135_s1));
  SHIFT_ADD shift_add_136 (
    .A2(shift_add_137_s1), .A3(shift_add_137_s2), .A0(A[1]), .A1(shift_add_137_s0), .S2(P0_3[3]),
    .S3(P4_7[0]), .S0(P0_3[1]), .S1(P0_3[2]));
  SHIFT_ADD shift_add_137 (
    .A2(shift_add_127_s1), .A3(shift_add_127_s2), .A0(A[2]), .A1(shift_add_127_s0), .S2(shift_add_137_s2),
    .S3(shift_add_137_s3), .S0(shift_add_137_s0), .S1(shift_add_137_s1));
  SHIFT_ADD shift_add_138 (
    .A2(shift_add_139_s1), .A3(shift_add_139_s2), .A0(shift_add_137_s3), .A1(shift_add_139_s0), .S2(P4_7[3]),
    .S3(P8_11[0]), .S0(P4_7[1]), .S1(P4_7[2]));
  SHIFT_ADD shift_add_139 (
    .A2(shift_add_128_s1), .A3(shift_add_128_s2), .A0(shift_add_127_s3), .A1(shift_add_128_s0),
    .S2(shift_add_139_s2), .S3(shift_add_139_s3), .S0(shift_add_139_s0), .S1(shift_add_139_s1));
  SHIFT_ADD shift_add_140 (
    .A2(shift_add_141_s1), .A3(shift_add_141_s2), .A0(shift_add_139_s3), .A1(shift_add_141_s0),
    .S2(P8_11[3]), .S3(P12_15[0]), .S0(P8_11[1]), .S1(P8_11[2]));
  SHIFT_ADD shift_add_141 (
    .A2(shift_add_129_s1), .A3(shift_add_129_s2), .A0(shift_add_128_s3), .A1(shift_add_129_s0),
    .S2(shift_add_141_s2), .S3(shift_add_141_s3), .S0(shift_add_141_s0), .S1(shift_add_141_s1));
  SHIFT_ADD shift_add_142 (
    .A2(shift_add_143_s1), .A3(shift_add_143_s2), .A0(shift_add_141_s3), .A1(shift_add_143_s0),
    .S2(P12_15[3]), .S3(P16_19[0]), .S0(P12_15[1]), .S1(P12_15[2]));
  SHIFT_ADD shift_add_143 (
    .A2(shift_add_130_s1), .A3(shift_add_130_s2), .A0(shift_add_129_s3), .A1(shift_add_130_s0),
    .S2(shift_add_143_s2), .S3(shift_add_143_s3), .S0(shift_add_143_s0), .S1(shift_add_143_s1));
  SHIFT_ADD shift_add_144 (
    .A2(shift_add_145_s1), .A3(shift_add_145_s2), .A0(shift_add_143_s3), .A1(shift_add_145_s0),
    .S2(P16_19[3]), .S3(P20_23[0]), .S0(P16_19[1]), .S1(P16_19[2]));
  SHIFT_ADD shift_add_145 (
    .A2(shift_add_131_s1), .A3(shift_add_131_s2), .A0(shift_add_130_s3), .A1(shift_add_131_s0),
    .S2(shift_add_145_s2), .S3(shift_add_145_s3), .S0(shift_add_145_s0), .S1(shift_add_145_s1));
  SHIFT_ADD shift_add_146 (
    .A2(shift_add_147_s1), .A3(shift_add_147_s2), .A0(shift_add_145_s3), .A1(shift_add_147_s0),
    .S2(P20_23[3]), .S3(P24_27[0]), .S0(P20_23[1]), .S1(P20_23[2]));
  SHIFT_ADD shift_add_147 (
    .A2(shift_add_132_s1), .A3(shift_add_132_s2), .A0(shift_add_131_s3), .A1(shift_add_132_s0),
    .S2(shift_add_147_s2), .S3(shift_add_147_s3), .S0(shift_add_147_s0), .S1(shift_add_147_s1));
  SHIFT_ADD shift_add_148 (
    .A2(shift_add_149_s1), .A3(shift_add_149_s2), .A0(shift_add_147_s3), .A1(shift_add_149_s0),
    .S2(P24_27[3]), .S3(P28_31[0]), .S0(P24_27[1]), .S1(P24_27[2]));
  SHIFT_ADD shift_add_149 (
    .A2(shift_add_133_s1), .A3(shift_add_133_s2), .A0(shift_add_132_s3), .A1(shift_add_133_s0),
    .S2(shift_add_149_s2), .S3(shift_add_149_s3), .S0(shift_add_149_s0), .S1(shift_add_149_s1));
  SHIFT_ADD shift_add_150 (
    .A2(shift_add_151_s1), .A3(shift_add_151_s2), .A0(shift_add_149_s3), .A1(shift_add_151_s0),
    .S2(P28_31[3]), .S3(P32_35[0]), .S0(P28_31[1]), .S1(P28_31[2]));
  SHIFT_ADD shift_add_151 (
    .A2(shift_add_134_s1), .A3(shift_add_134_s2), .A0(shift_add_133_s3), .A1(shift_add_134_s0),
    .S2(shift_add_151_s2), .S3(shift_add_151_s3), .S0(shift_add_151_s0), .S1(shift_add_151_s1));
  SHIFT_ADD shift_add_152 (
    .A2(shift_add_153_s1), .A3(shift_add_153_s2), .A0(shift_add_151_s3), .A1(shift_add_153_s0),
    .S2(P32_35[3]), .S3(P36_39[0]), .S0(P32_35[1]), .S1(P32_35[2]));
  SHIFT_ADD shift_add_153 (
    .A2(shift_add_135_s1), .A3(shift_add_135_s2), .A0(shift_add_134_s3), .A1(shift_add_135_s0),
    .S2(shift_add_153_s2), .S3(shift_add_153_s3), .S0(shift_add_153_s0), .S1(shift_add_153_s1));
  SHIFT_ADD shift_add_154 (
    .A2(shift_add_155_s1), .A3(shift_add_155_s2), .A0(shift_add_153_s3), .A1(shift_add_155_s0),
    .S2(P36_39[3]), .S0(P36_39[1]), .S1(P36_39[2]));  // open: S3
  SHIFT_ADD shift_add_155 (
    .A2(shift_add_117_s3), .A3(1'b0), .A0(shift_add_135_s3), .A1(shift_add_126_s3), .S2(shift_add_155_s2),
    .S0(shift_add_155_s0), .S1(shift_add_155_s1));  // open: S3

  assign P0_3[0] = A[0];
endmodule

module HEX_DISP_DEC (
  input  E,
  input  [3:0] BIN,
  output [8:0] L0,
  output [8:0] L1,
  output [8:0] L2,
  output [8:0] L3,
  output [8:0] L4
);

  PLA #(.in_width(5), .out_width(45), .\table ("0xxx1 110000011010000000000000000110000001110000000 # EXEMPLE\n0xxxx 000000000000000000000000000000000000000000000 # DISABLE\n10000 011111110100000001100010001100000001011111110 # 0\n10001 000000000000000000111111111010000000000000000 # 1\n10010 011000001100100001100010001100001101010000011 # 2\n10011 011101110100010001100010001100010001010000010 # 3\n10100 011111111000001000000001000111001000000111000 # 4\n10101 100011110100010001100010001100010001111110010 # 5\n10110 010001110100010001100010001100010001011111110 # 6\n10111 111000000100110000100001111100000000100000000 # 7\n11000 011101110100010001100010001100010001011101110 # 8\n11001 011111110100010001100010001100010001011100010 # 9\n11010 011111111100010000100010000100010000011111111 # A\n11011 011101110100010001100010001100010001111111111 # B\n11100 010000010100000001100000001100000001011111110 # C\n11101 011111110100000001100000001100000001111111111 # D\n11110 100000001100010001100010001100010001111111111 # E\n11111 100000000100010000100010000100010000111111111 # F")) pla_1 (
    .in({E, BIN}), .out({L4, L3, L2, L1, L0}));
  LED HEX_DEC_ENABLE (.in(E));
endmodule

module DEC_DISP_DEC (
  input  En,
  input  [3:0] X,
  output A,
  output B,
  output C,
  output D,
  output E,
  output F,
  output G
);

  PLA #(.in_width(5), .out_width(7), .\table ("0xxxx 0000000 # DISABLE\n10000 0111111 # 0\n10001 0000110 # 1\n10010 1011011 # 2\n10011 1001111 # 3\n10100 1100110 # 4\n10101 1101101 # 5\n10110 1111101 # 6\n10111 0000111 # 7\n11000 1111111 # 8\n11001 1101111 # 9")) pla_1 (
    .in({En, X}), .out({G, F, E, D, C, B, A}));
endmodule

module HEX_DISP_16b (
  input  [15:0] A
);

  Hex_Digit_Display #(.decimalPoint("false")) hex_digit_display_1 (.value(A[15:12]));
  Hex_Digit_Display #(.decimalPoint("false")) hex_digit_display_2 (.value(A[11:8]));
  Hex_Digit_Display #(.decimalPoint("false")) hex_digit_display_3 (.value(A[7:4]));
  Hex_Digit_Display #(.decimalPoint("false")) hex_digit_display_4 (.value(A[3:0]));
endmodule

module T_BOX (
  input  T,
  output S
);

  T_Flip_Flop t_ff_1 (.clk(T), .T(T), .Q(S));  // open: Qn, preset, reset
  LED led_1 (.in(S));
endmodule
